// Logisim project 1st_project.circ as structural Verilog: 1 circuit, main circuit main
module main (
  input  in_1
);

  wire CLOCK, comparator_1_eq, comparator_2_eq, comparator_3_eq, comparator_4_eq, comparator_5_eq,
       j_k_ff_1_q, j_k_ff_2_q, n7_segment_display_1_p1, n7_segment_display_2_p1, n7_segment_display_3_p1;
  wire [7:0] counter_1_q;

  Clock clock_1 (.out(CLOCK));
  Counter #(.max('hf)) counter_1 (.clr(in_1), .clk(CLOCK), .Q(counter_1_q));  // open: load, up, count, D, carry
  // BCD_to_7_Segment_decoder bcd_to_7_segment_decoder_1: pin names not known
  // _7_Segment_Display 7_segment_display_1: pin names not known; wires that end beside it: n7_segment_display_1_p1, n7_segment_display_1_p1
  // Binary_to_BCD_converter #(.binvalue(8)) binary_to_bcd_converter_1: pin names not known; wires that end beside it: counter_1_q
  Comparator comparator_1 (.a({8{1'b0}}), .b(counter_1_q), .eq(comparator_1_eq));  // open: gt, lt
  Comparator comparator_2 (.a(8'h2), .b(counter_1_q), .eq(comparator_2_eq));  // open: gt, lt
  Comparator comparator_3 (.a(8'ha), .b(counter_1_q), .eq(comparator_3_eq));  // open: gt, lt
  Comparator comparator_4 (.a(8'h5), .b(counter_1_q), .eq(comparator_4_eq));  // open: gt, lt
  Comparator comparator_5 (.a(8'ha), .b(counter_1_q), .eq(comparator_5_eq));  // open: gt, lt
  // BCD_to_7_Segment_decoder bcd_to_7_segment_decoder_2: pin names not known
  // BCD_to_7_Segment_decoder bcd_to_7_segment_decoder_3: pin names not known
  // _7_Segment_Display 7_segment_display_2: pin names not known; wires that end beside it: n7_segment_display_2_p1, n7_segment_display_2_p1
  // _7_Segment_Display 7_segment_display_3: pin names not known; wires that end beside it: n7_segment_display_3_p1, n7_segment_display_3_p1
  LED led_1 (.in(comparator_1_eq));
  J_K_Flip_Flop j_k_ff_1 (
    .J(comparator_2_eq), .K(comparator_3_eq), .clk(CLOCK), .Q(j_k_ff_1_q));  // open: Qn, preset, reset
  J_K_Flip_Flop j_k_ff_2 (
    .J(comparator_4_eq), .K(comparator_5_eq), .clk(CLOCK), .Q(j_k_ff_2_q));  // open: Qn, preset, reset
  // Buzzer buzzer_1: pin names not known; wires that end beside it: 14'h215, comparator_1_eq
  // Buzzer buzzer_2: pin names not known; wires that end beside it: 14'h1066, j_k_ff_2_q
  // Buzzer buzzer_3: pin names not known; wires that end beside it: 14'h320, j_k_ff_1_q
  // Digital_Oscilloscope digital_oscilloscope_1: pin names not known; wires that end beside it: CLOCK, comparator_1_eq, j_k_ff_1_q, j_k_ff_2_q
endmodule
