// Logisim project ALU.circ as structural Verilog
// NOT
module main (
  input  A,
  output result
);

  Transistor transistor_1 (.in(1'b1), .out(result), .gate(A));
  Transistor #(.\type ("n")) transistor_2 (.in(1'b0), .out(result), .gate(A));
endmodule

module NOT_GATE (
  input  in_1,
  output out_2
);

  Transistor transistor_1 (.in(1'b1), .out(out_2), .gate(in_1));
  Transistor #(.\type ("n")) transistor_2 (.in(1'b0), .out(out_2), .gate(in_1));
endmodule

module NAND_GATE (
  input  A,
  input  B,
  output result
);

  wire transistor_4_out;

  Transistor transistor_1 (.in(1'b1), .out(result), .gate(A));
  Transistor transistor_2 (.in(1'b1), .out(result), .gate(B));
  Transistor #(.\type ("n")) transistor_3 (.in(transistor_4_out), .out(result), .gate(A));
  Transistor #(.\type ("n")) transistor_4 (.in(1'b0), .out(transistor_4_out), .gate(B));
endmodule

module AND_GATE (
  input  A,
  input  B,
  output result
);

  wire transistor_1_out, transistor_3_out;

  Transistor transistor_1 (.in(1'b1), .out(transistor_1_out), .gate(B));
  Transistor #(.\type ("n")) transistor_2 (.in(transistor_3_out), .out(transistor_1_out), .gate(B));
  Transistor #(.\type ("n")) transistor_3 (.in(1'b0), .out(transistor_3_out), .gate(A));
  Transistor transistor_4 (.in(1'b1), .out(transistor_1_out), .gate(A));
  Transistor transistor_5 (.in(1'b1), .out(result), .gate(transistor_1_out));
  Transistor #(.\type ("n")) transistor_6 (.in(1'b0), .out(result), .gate(transistor_1_out));
endmodule

module NOR_GATE (
  input  A,
  input  B,
  output result
);

  wire transistor_1_out;

  Transistor transistor_1 (.in(1'b1), .out(transistor_1_out), .gate(A));
  Transistor transistor_2 (.in(transistor_1_out), .out(result), .gate(B));
  Transistor #(.\type ("n")) transistor_3 (.in(1'b0), .out(result), .gate(A));
  Transistor #(.\type ("n")) transistor_4 (.in(1'b0), .out(result), .gate(B));
endmodule

module OR_GATE (
  input  A,
  input  B,
  output out_3
);

  wire transistor_1_out, transistor_2_out;

  Transistor #(.\type ("n")) transistor_1 (.in(1'b0), .out(transistor_1_out), .gate(A));
  Transistor transistor_2 (.in(1'b1), .out(transistor_2_out), .gate(A));
  Transistor transistor_3 (.in(transistor_2_out), .out(transistor_1_out), .gate(B));
  Transistor #(.\type ("n")) transistor_4 (.in(1'b0), .out(transistor_1_out), .gate(B));
  Transistor transistor_5 (.in(1'b1), .out(out_3), .gate(transistor_1_out));
  Transistor #(.\type ("n")) transistor_6 (.in(1'b0), .out(out_3), .gate(transistor_1_out));
endmodule

module XOR_GATE (
  input  A,
  input  B,
  output result
);

  wire nand_gate_1_result, nand_gate_2_result, nand_gate_3_result;

  NAND_GATE nand_gate_1 (.A(A), .B(B), .result(nand_gate_1_result));
  NAND_GATE nand_gate_2 (.A(A), .B(nand_gate_1_result), .result(nand_gate_2_result));
  NAND_GATE nand_gate_3 (.A(nand_gate_1_result), .B(B), .result(nand_gate_3_result));
  NAND_GATE nand_gate_4 (.A(nand_gate_2_result), .B(nand_gate_3_result), .result(result));
endmodule

module XNOR_GATE (
  input  A,
  input  B,
  output result
);

  wire xor_gate_1_result;

  XOR_GATE xor_gate_1 (.A(A), .B(B), .result(xor_gate_1_result));
  NOT_GATE not_gate_1 (.in_1(xor_gate_1_result), .out_2(result));
endmodule

module HALF_ADDER (
  input  A,
  input  B,
  output sum,
  output carry
);

  XOR_GATE xor_gate_1 (.A(A), .B(B), .result(sum));
  AND_GATE and_gate_1 (.A(A), .B(B), .result(carry));
endmodule

module ODD (
  input  A,
  input  B,
  input  CARRY_IN,
  output SUM
);

  wire xor_gate_1_result;

  XOR_GATE xor_gate_1 (.A(A), .B(B), .result(xor_gate_1_result));
  XOR_GATE xor_gate_2 (.A(xor_gate_1_result), .B(CARRY_IN), .result(SUM));
endmodule

module MAJ (
  input  A,
  input  B,
  input  CARRY_IN,
  output result
);

  wire and_gate_1_result, and_gate_2_result, xor_gate_1_result;

  AND_GATE and_gate_1 (.A(A), .B(B), .result(and_gate_1_result));
  XOR_GATE xor_gate_1 (.A(A), .B(B), .result(xor_gate_1_result));
  AND_GATE and_gate_2 (.A(xor_gate_1_result), .B(CARRY_IN), .result(and_gate_2_result));
  OR_GATE or_gate_1 (.A(and_gate_1_result), .B(and_gate_2_result), .out_3(result));
endmodule

module Full_adder (
  input  A,
  input  B,
  input  CARRY_IN,
  output SUM,
  output CARRY_OUT
);

  ODD odd_1 (.A(A), .B(B), .CARRY_IN(CARRY_IN), .SUM(SUM));
  MAJ maj_1 (.A(A), .B(B), .CARRY_IN(CARRY_IN), .result(CARRY_OUT));
endmodule

module ADDER_8_BIT (
  input  [7:0] A,
  input  carry,
  input  [7:0] B,
  output [7:0] SUM,
  output Carry_out
);

  wire full_adder_1_carry_out, full_adder_2_carry_out, full_adder_3_carry_out, full_adder_4_carry_out,
       full_adder_5_carry_out, full_adder_6_carry_out, full_adder_7_carry_out;

  // Probe on A
  // Probe on B
  Full_adder full_adder_1 (.A(A[0]), .B(B[0]), .CARRY_IN(carry), .SUM(SUM[0]), .CARRY_OUT(full_adder_1_carry_out));
  Full_adder full_adder_2 (
    .A(A[1]), .B(B[1]), .CARRY_IN(full_adder_1_carry_out), .SUM(SUM[1]), .CARRY_OUT(full_adder_2_carry_out));
  Full_adder full_adder_3 (
    .A(A[2]), .B(B[2]), .CARRY_IN(full_adder_2_carry_out), .SUM(SUM[2]), .CARRY_OUT(full_adder_3_carry_out));
  Full_adder full_adder_4 (
    .A(A[3]), .B(B[3]), .CARRY_IN(full_adder_3_carry_out), .SUM(SUM[3]), .CARRY_OUT(full_adder_4_carry_out));
  Full_adder full_adder_5 (
    .A(A[4]), .B(B[4]), .CARRY_IN(full_adder_4_carry_out), .SUM(SUM[4]), .CARRY_OUT(full_adder_5_carry_out));
  Full_adder full_adder_6 (
    .A(A[5]), .B(B[5]), .CARRY_IN(full_adder_5_carry_out), .SUM(SUM[5]), .CARRY_OUT(full_adder_6_carry_out));
  Full_adder full_adder_7 (
    .A(A[6]), .B(B[6]), .CARRY_IN(full_adder_6_carry_out), .SUM(SUM[6]), .CARRY_OUT(full_adder_7_carry_out));
  Full_adder full_adder_8 (.A(A[7]), .B(B[7]), .CARRY_IN(full_adder_7_carry_out), .SUM(SUM[7]), .CARRY_OUT(Carry_out));
  // Probe on SUM
endmodule

module AND_8BIT (
  input  [7:0] A,
  input  [7:0] B,
  output [7:0] result
);

  AND_GATE and_gate_1 (.A(A[0]), .B(B[0]), .result(result[0]));
  AND_GATE and_gate_2 (.A(A[1]), .B(B[1]), .result(result[1]));
  AND_GATE and_gate_3 (.A(A[2]), .B(B[2]), .result(result[2]));
  AND_GATE and_gate_4 (.A(A[3]), .B(B[3]), .result(result[3]));
  AND_GATE and_gate_5 (.A(A[4]), .B(B[4]), .result(result[4]));
  AND_GATE and_gate_6 (.A(A[5]), .B(B[5]), .result(result[5]));
  AND_GATE and_gate_7 (.A(A[6]), .B(B[6]), .result(result[6]));
  AND_GATE and_gate_8 (.A(A[7]), .B(B[7]), .result(result[7]));
endmodule

module XOR_8BIT (
  input  [7:0] A,
  input  [7:0] B,
  output [7:0] result
);

  XOR_GATE xor_gate_1 (.A(A[0]), .B(B[0]), .result(result[0]));
  XOR_GATE xor_gate_2 (.A(A[1]), .B(B[1]), .result(result[1]));
  XOR_GATE xor_gate_3 (.A(A[2]), .B(B[2]), .result(result[2]));
  XOR_GATE xor_gate_4 (.A(A[3]), .B(B[3]), .result(result[3]));
  XOR_GATE xor_gate_5 (.A(A[4]), .B(B[4]), .result(result[4]));
  XOR_GATE xor_gate_6 (.A(A[5]), .B(B[5]), .result(result[5]));
  XOR_GATE xor_gate_7 (.A(A[6]), .B(B[6]), .result(result[6]));
  XOR_GATE xor_gate_8 (.A(A[7]), .B(B[7]), .result(result[7]));
endmodule

module AND_3INPUT (
  input  A,
  input  B,
  input  C,
  output RESULT
);

  wire and_gate_1_result;

  AND_GATE and_gate_1 (.A(A), .B(B), .result(and_gate_1_result));
  AND_GATE and_gate_2 (.A(and_gate_1_result), .B(C), .result(RESULT));
endmodule

module decorder3_8 (
  input  A,
  input  B,
  input  C,
  output s1,
  output s2,
  output s3,
  output s4,
  output s5,
  output s6,
  output s7,
  output s8
);

  wire not_gate_1_out_2, not_gate_2_out_2, not_gate_3_out_2;

  NOT_GATE not_gate_1 (.in_1(A), .out_2(not_gate_1_out_2));
  NOT_GATE not_gate_2 (.in_1(B), .out_2(not_gate_2_out_2));
  NOT_GATE not_gate_3 (.in_1(C), .out_2(not_gate_3_out_2));
  AND_3INPUT and_3input_1 (.A(not_gate_1_out_2), .B(not_gate_2_out_2), .C(not_gate_3_out_2), .RESULT(s1));
  AND_3INPUT and_3input_2 (.A(not_gate_1_out_2), .B(not_gate_2_out_2), .C(C), .RESULT(s2));
  AND_3INPUT and_3input_3 (.A(not_gate_1_out_2), .B(B), .C(not_gate_3_out_2), .RESULT(s3));
  AND_3INPUT and_3input_4 (.A(not_gate_1_out_2), .B(B), .C(C), .RESULT(s4));
  AND_3INPUT and_3input_5 (.A(A), .B(not_gate_2_out_2), .C(not_gate_3_out_2), .RESULT(s5));
  AND_3INPUT and_3input_6 (.A(A), .B(not_gate_2_out_2), .C(C), .RESULT(s6));
  AND_3INPUT and_3input_7 (.A(A), .B(B), .C(not_gate_3_out_2), .RESULT(s7));
  AND_3INPUT and_3input_8 (.A(A), .B(B), .C(C), .RESULT(s8));
endmodule

module demux3_8 (
  input  Singal,
  input  A,
  input  B,
  input  C,
  output s1,
  output s2,
  output s3,
  output s4,
  output s5,
  output s6,
  output s7,
  output s8
);

  wire decorder3_8_1_s1, decorder3_8_1_s2, decorder3_8_1_s3, decorder3_8_1_s4, decorder3_8_1_s5,
       decorder3_8_1_s6, decorder3_8_1_s7, decorder3_8_1_s8;

  decorder3_8 decorder3_8_1 (
    .A(A), .B(B), .C(C), .s1(decorder3_8_1_s1), .s2(decorder3_8_1_s2), .s3(decorder3_8_1_s3),
    .s4(decorder3_8_1_s4), .s5(decorder3_8_1_s5), .s6(decorder3_8_1_s6), .s7(decorder3_8_1_s7),
    .s8(decorder3_8_1_s8));
  AND_GATE and_gate_1 (.A(decorder3_8_1_s1), .B(Singal), .result(s1));
  AND_GATE and_gate_2 (.A(decorder3_8_1_s2), .B(Singal), .result(s2));
  AND_GATE and_gate_3 (.A(decorder3_8_1_s3), .B(Singal), .result(s3));
  AND_GATE and_gate_4 (.A(decorder3_8_1_s4), .B(Singal), .result(s4));
  AND_GATE and_gate_5 (.A(decorder3_8_1_s5), .B(Singal), .result(s5));
  AND_GATE and_gate_6 (.A(decorder3_8_1_s6), .B(Singal), .result(s6));
  AND_GATE and_gate_7 (.A(decorder3_8_1_s7), .B(Singal), .result(s7));
  AND_GATE and_gate_8 (.A(decorder3_8_1_s8), .B(Singal), .result(s8));
endmodule

module decordANDmux (
  input  DATA_IN,
  input  A,
  input  B,
  input  C,
  output S1_1,
  output S1_X,
  output S2_1,
  output S2_X,
  output S3_1,
  output S3_X,
  output S4_1,
  output S4_X,
  output S5_1,
  output S5_X,
  output S6_1,
  output S6_X,
  output S7_1,
  output S7_X,
  output S8_1,
  output S8_X
);

  decorder3_8 decorder3_8_1 (
    .A(A), .B(B), .C(C), .s1(S1_1), .s2(S2_1), .s3(S3_1), .s4(S4_1), .s5(S5_1), .s6(S6_1), .s7(S7_1),
    .s8(S8_1));
  AND_GATE and_gate_1 (.A(S1_1), .B(DATA_IN), .result(S1_X));
  AND_GATE and_gate_2 (.A(S2_1), .B(DATA_IN), .result(S2_X));
  AND_GATE and_gate_3 (.A(S3_1), .B(DATA_IN), .result(S3_X));
  AND_GATE and_gate_4 (.A(S4_1), .B(DATA_IN), .result(S4_X));
  AND_GATE and_gate_5 (.A(S5_1), .B(DATA_IN), .result(S5_X));
  AND_GATE and_gate_6 (.A(S6_1), .B(DATA_IN), .result(S6_X));
  AND_GATE and_gate_7 (.A(S7_1), .B(DATA_IN), .result(S7_X));
  AND_GATE and_gate_8 (.A(S8_1), .B(DATA_IN), .result(S8_X));
endmodule

module OR_8BIT (
  input  [7:0] A,
  input  [7:0] B,
  output [7:0] Result
);

  OR_GATE or_gate_1 (.A(A[0]), .B(B[0]), .out_3(Result[0]));
  OR_GATE or_gate_2 (.A(A[1]), .B(B[1]), .out_3(Result[1]));
  OR_GATE or_gate_3 (.A(A[2]), .B(B[2]), .out_3(Result[2]));
  OR_GATE or_gate_4 (.A(A[3]), .B(B[3]), .out_3(Result[3]));
  OR_GATE or_gate_5 (.A(A[4]), .B(B[4]), .out_3(Result[4]));
  OR_GATE or_gate_6 (.A(A[5]), .B(B[5]), .out_3(Result[5]));
  OR_GATE or_gate_7 (.A(A[6]), .B(B[6]), .out_3(Result[6]));
  OR_GATE or_gate_8 (.A(A[7]), .B(B[7]), .out_3(Result[7]));
endmodule

module OR_3input (
  input  [7:0] A,
  input  [7:0] B,
  input  [7:0] C,
  output [7:0] result
);

  wire [7:0] or_8bit_1_result;

  OR_8BIT or_8bit_1 (.A(A), .B(B), .Result(or_8bit_1_result));
  OR_8BIT or_8bit_2 (.A(or_8bit_1_result), .B(C), .Result(result));
endmodule

module ONE_hot_mux (
  input  add,
  input  sub,
  input  xor_b,
  input  and_b,
  input  r_shift,
  input  l_shift,
  input  sel_add,
  input  sel_sub,
  input  sel_xor,
  input  sel_and,
  input  sel_Rshift,
  input  sel_Lshift,
  output mux_out
);

  wire and_gate_1_result, and_gate_2_result, and_gate_3_result, and_gate_4_result, and_gate_5_result,
       and_gate_6_result;

  AND_GATE and_gate_1 (.A(add), .B(sel_add), .result(and_gate_1_result));
  AND_GATE and_gate_2 (.A(sub), .B(sel_sub), .result(and_gate_2_result));
  AND_GATE and_gate_3 (.A(xor_b), .B(sel_xor), .result(and_gate_3_result));
  AND_GATE and_gate_4 (.A(and_b), .B(sel_and), .result(and_gate_4_result));
  AND_GATE and_gate_5 (.A(r_shift), .B(sel_Rshift), .result(and_gate_5_result));
  AND_GATE and_gate_6 (.A(l_shift), .B(sel_Lshift), .result(and_gate_6_result));
  or or_1 (mux_out, and_gate_1_result, and_gate_2_result, and_gate_3_result, and_gate_4_result, and_gate_5_result, and_gate_6_result);
endmodule

module hot_8_mux (
  input  sel_add,
  input  sel_sub,
  input  sel_xor,
  input  sel_and,
  input  sel_Rshift,
  input  sel_Lshift,
  input  [7:0] add,
  input  [7:0] l_shift,
  input  [7:0] and_b,
  input  [7:0] r_shift,
  input  [7:0] sub,
  input  [7:0] xor_in,
  output [7:0] resul
);

  ONE_hot_mux one_hot_mux_1 (
    .add(add[0]), .sub(sub[0]), .xor_b(xor_in[0]), .and_b(and_b[0]), .r_shift(r_shift[0]),
    .l_shift(l_shift[0]), .sel_add(sel_add), .sel_sub(sel_sub), .sel_xor(sel_xor), .sel_and(sel_and),
    .sel_Rshift(sel_Rshift), .sel_Lshift(sel_Lshift), .mux_out(resul[0]));
  ONE_hot_mux one_hot_mux_2 (
    .add(add[1]), .sub(sub[1]), .xor_b(xor_in[1]), .and_b(and_b[1]), .r_shift(r_shift[1]),
    .l_shift(l_shift[1]), .sel_add(sel_add), .sel_sub(sel_sub), .sel_xor(sel_xor), .sel_and(sel_and),
    .sel_Rshift(sel_Rshift), .sel_Lshift(sel_Lshift), .mux_out(resul[1]));
  ONE_hot_mux one_hot_mux_3 (
    .add(add[2]), .sub(sub[2]), .xor_b(xor_in[2]), .and_b(and_b[2]), .r_shift(r_shift[2]),
    .l_shift(l_shift[2]), .sel_add(sel_add), .sel_sub(sel_sub), .sel_xor(sel_xor), .sel_and(sel_and),
    .sel_Rshift(sel_Rshift), .sel_Lshift(sel_Lshift), .mux_out(resul[2]));
  ONE_hot_mux one_hot_mux_4 (
    .add(add[3]), .sub(sub[3]), .xor_b(xor_in[3]), .and_b(and_b[3]), .r_shift(r_shift[3]),
    .l_shift(l_shift[3]), .sel_add(sel_add), .sel_sub(sel_sub), .sel_xor(sel_xor), .sel_and(sel_and),
    .sel_Rshift(sel_Rshift), .sel_Lshift(sel_Lshift), .mux_out(resul[3]));
  ONE_hot_mux one_hot_mux_5 (
    .add(add[4]), .sub(sub[4]), .xor_b(xor_in[4]), .and_b(and_b[4]), .r_shift(r_shift[4]),
    .l_shift(l_shift[4]), .sel_add(sel_add), .sel_sub(sel_sub), .sel_xor(sel_xor), .sel_and(sel_and),
    .sel_Rshift(sel_Rshift), .sel_Lshift(sel_Lshift), .mux_out(resul[4]));
  ONE_hot_mux one_hot_mux_6 (
    .add(add[5]), .sub(sub[5]), .xor_b(xor_in[5]), .and_b(and_b[5]), .r_shift(r_shift[5]),
    .l_shift(l_shift[5]), .sel_add(sel_add), .sel_sub(sel_sub), .sel_xor(sel_xor), .sel_and(sel_and),
    .sel_Rshift(sel_Rshift), .sel_Lshift(sel_Lshift), .mux_out(resul[5]));
  ONE_hot_mux one_hot_mux_7 (
    .add(add[6]), .sub(sub[6]), .xor_b(xor_in[6]), .and_b(and_b[6]), .r_shift(r_shift[6]),
    .l_shift(l_shift[6]), .sel_add(sel_add), .sel_sub(sel_sub), .sel_xor(sel_xor), .sel_and(sel_and),
    .sel_Rshift(sel_Rshift), .sel_Lshift(sel_Lshift), .mux_out(resul[6]));
  ONE_hot_mux one_hot_mux_8 (
    .add(add[7]), .sub(sub[7]), .xor_b(xor_in[7]), .and_b(and_b[7]), .r_shift(r_shift[7]),
    .l_shift(l_shift[7]), .sel_add(sel_add), .sel_sub(sel_sub), .sel_xor(sel_xor), .sel_and(sel_and),
    .sel_Rshift(sel_Rshift), .sel_Lshift(sel_Lshift), .mux_out(resul[7]));
endmodule

module l_shift (
  input  carry_in,
  input  [7:0] A,
  output carry_Out,
  output [7:0] result
);


  assign carry_Out = A[7];
  assign result = {A[6:0], carry_in};
endmodule

module R_shift (
  input  [7:0] A,
  input  Carry_in,
  output carry_out,
  output [7:0] result
);


  assign carry_out = A[0];
  assign result = {Carry_in, A[7:1]};
endmodule

module sub_8 (
  input  [7:0] A,
  input  carry_in,
  input  [7:0] B,
  output [7:0] result,
  output borrow
);

  wire [7:0] xor_8bit_1_result;

  XOR_8BIT xor_8bit_1 (.A(B), .B({8{1'b1}}), .result(xor_8bit_1_result));
  ADDER_8_BIT adder_8_bit_1 (.A(A), .carry(carry_in), .B(xor_8bit_1_result), .SUM(result), .Carry_out(borrow));
endmodule

module MILESTONE (
  input  [7:0] A,
  input  [7:0] B,
  input  add,
  input  sub,
  input  xor_r,
  input  AND_R,
  input  r_shift_r,
  input  L_shift_r,
  output [7:0] result
);

  wire [7:0] adder_8_bit_1_sum, and_8bit_1_result, l_shift_1_result, r_shift_1_result, sub_8_1_result,
       xor_8bit_1_result;

  // Probe on A
  // Probe on B
  ADDER_8_BIT adder_8_bit_1 (.A(A), .B(B), .SUM(adder_8_bit_1_sum));  // open: carry, Carry_out
  sub_8 sub_8_1 (.A(A), .B(B), .result(sub_8_1_result));  // open: carry_in, borrow
  XOR_8BIT xor_8bit_1 (.A(A), .B(B), .result(xor_8bit_1_result));
  AND_8BIT and_8bit_1 (.A(A), .B(B), .result(and_8bit_1_result));
  R_shift r_shift_1 (.A(A), .result(r_shift_1_result));  // open: Carry_in, carry_out
  l_shift l_shift_1 (.A(A), .result(l_shift_1_result));  // open: carry_in, carry_Out
  hot_8_mux hot_8_mux_1 (
    .sel_add(add), .sel_sub(sub), .sel_xor(xor_r), .sel_and(AND_R), .sel_Rshift(r_shift_r),
    .sel_Lshift(L_shift_r), .add(adder_8_bit_1_sum), .l_shift(l_shift_1_result), .and_b(and_8bit_1_result),
    .r_shift(r_shift_1_result), .sub(sub_8_1_result), .xor_in(xor_8bit_1_result), .resul(result));
  // Probe on result
endmodule

module FINAL (
  input  [7:0] A,
  input  [7:0] B,
  input  ADD,
  input  SUB,
  input  XOR_r,
  input  AND_r,
  input  R_shift_r,
  input  L_shift_l,
  output [7:0] out_9
);

  // Probe on A
  // Probe on B
  MILESTONE milestone_1 (
    .A(A), .B(B), .add(ADD), .sub(SUB), .xor_r(XOR_r), .AND_R(AND_r), .r_shift_r(R_shift_r),
    .L_shift_r(L_shift_l), .result(out_9));
  // Probe on out_9
endmodule

module srlatch (
  input  S,
  input  R,
  output out_3
);

  wire nor_2_out;

  nor nor_1 (out_3, S, nor_2_out);
  nor nor_2 (nor_2_out, R, out_3);
endmodule

module flipflop (
  input  Data,
  input  CLK,
  output Q
);

  wire nand_1_out, nand_2_out, not_1_out;

  not not_1 (not_1_out, Data);
  nand nand_1 (nand_1_out, Data, CLK);
  nand nand_2 (nand_2_out, not_1_out, CLK);
  srlatch srlatch_1 (.S(nand_1_out), .R(nand_2_out), .out_3(Q));
endmodule

module memoryclk (
  input  enable,
  input  new_data,
  input  CLK,
  output Q
);

  wire and_1_out, and_2_out, not_1_out, or_1_out;

  not not_1 (not_1_out, enable);
  and and_1 (and_1_out, new_data, enable);
  and and_2 (and_2_out, Q, not_1_out);
  or or_1 (or_1_out, and_1_out, and_2_out);
  D_Flip_Flop d_ff_1 (.D(or_1_out), .clk(CLK), .Q(Q));  // open: Qn, preset, reset
endmodule

module memotybit (
  input  DATA,
  input  CLK,
  output out_3
);

  wire and_1_out, and_2_out, not_1_out;

  not not_1 (not_1_out, DATA);
  and and_1 (and_1_out, CLK, not_1_out);
  and and_2 (and_2_out, DATA, CLK);
  srlatch srlatch_1 (.S(and_1_out), .R(and_2_out), .out_3(out_3));
endmodule

module clock_control (
  input  RUN,
  input  halt,
  output Cl,
  output fetch,
  output fetch_w,
  output execute,
  output execute_w
);

  wire clock_1_out, not_1_out;

  Clock clock_1 (.out(clock_1_out));
  and and_1 (Cl, RUN, clock_1_out, halt);
  D_Flip_Flop d_ff_1 (.D(not_1_out), .clk(Cl), .Q(execute));  // open: Qn, preset, reset
  not not_1 (not_1_out, execute);
  not not_2 (fetch, execute);
  and and_2 (fetch_w, fetch, Cl);
  and and_3 (execute_w, execute, Cl);
endmodule

module reg8bit (
  input  write,
  input  [7:0] Data,
  input  clk,
  output [7:0] Q
);

  memoryclk memoryclk_1 (.enable(write), .new_data(Data[6]), .CLK(clk), .Q(Q[6]));
  memoryclk memoryclk_2 (.enable(write), .new_data(Data[0]), .CLK(clk), .Q(Q[0]));
  memoryclk memoryclk_3 (.enable(write), .new_data(Data[1]), .CLK(clk), .Q(Q[1]));
  memoryclk memoryclk_4 (.enable(write), .new_data(Data[2]), .CLK(clk), .Q(Q[2]));
  memoryclk memoryclk_5 (.enable(write), .new_data(Data[3]), .CLK(clk), .Q(Q[3]));
  memoryclk memoryclk_6 (.enable(write), .new_data(Data[4]), .CLK(clk), .Q(Q[4]));
  memoryclk memoryclk_7 (.enable(write), .new_data(Data[5]), .CLK(clk), .Q(Q[5]));
  memoryclk memoryclk_8 (.enable(write), .new_data(Data[7]), .CLK(clk), .Q(Q[7]));
endmodule

module reg4bit (
  input  enable,
  input  [3:0] new_data,
  input  clk,
  output [3:0] Q
);

  memoryclk memoryclk_1 (.enable(enable), .new_data(new_data[0]), .CLK(clk), .Q(Q[0]));
  memoryclk memoryclk_2 (.enable(enable), .new_data(new_data[1]), .CLK(clk), .Q(Q[1]));
  memoryclk memoryclk_3 (.enable(enable), .new_data(new_data[2]), .CLK(clk), .Q(Q[2]));
  memoryclk memoryclk_4 (.enable(enable), .new_data(new_data[3]), .CLK(clk), .Q(Q[3]));
endmodule

module Incrementer4bit (
  input  [7:0] PC_input,
  output [7:0] r
);

  wire and_2_out, and_3_out, and_4_out, and_5_out, and_6_out, and_7_out, and_8_out;

  xor xor_1 (r[7], and_8_out, PC_input[7]);
  // AND_Gate and_1 has open pins: in0=PC_input[7], in1=and_8_out, out=open
  xor xor_2 (r[4], and_3_out, PC_input[4]);
  and and_2 (and_2_out, PC_input[4], and_3_out);
  xor xor_3 (r[3], and_4_out, PC_input[3]);
  and and_3 (and_3_out, PC_input[3], and_4_out);
  xor xor_4 (r[2], and_5_out, PC_input[2]);
  and and_4 (and_4_out, PC_input[2], and_5_out);
  xor xor_5 (r[1], and_6_out, PC_input[1]);
  and and_5 (and_5_out, PC_input[1], and_6_out);
  xor xor_6 (r[0], PC_input[0], 1'b1);
  and and_6 (and_6_out, PC_input[0], 1'b1);
  xor xor_7 (r[5], and_2_out, PC_input[5]);
  and and_7 (and_7_out, PC_input[5], and_2_out);
  xor xor_8 (r[6], and_7_out, PC_input[6]);
  and and_8 (and_8_out, PC_input[6], and_7_out);
endmodule

module BusMux2waybit1 (
  input  Incrementer,
  input  PC_LOAD,
  input  Branch_Address,
  output result
);

  wire and_1_out, and_2_out, not_1_out;

  not not_1 (not_1_out, PC_LOAD);
  and and_1 (and_1_out, Incrementer, not_1_out);
  and and_2 (and_2_out, Branch_Address, PC_LOAD);
  or or_1 (result, and_1_out, and_2_out);
endmodule

module BusMux2way (
  input  S,
  input  [3:0] increment,
  input  [3:0] Branch,
  output [3:0] result
);

  BusMux2waybit1 busmux2waybit1_1 (
    .Incrementer(increment[0]), .PC_LOAD(S), .Branch_Address(Branch[0]), .result(result[0]));
  BusMux2waybit1 busmux2waybit1_2 (
    .Incrementer(increment[1]), .PC_LOAD(S), .Branch_Address(Branch[1]), .result(result[1]));
  BusMux2waybit1 busmux2waybit1_3 (
    .Incrementer(increment[2]), .PC_LOAD(S), .Branch_Address(Branch[2]), .result(result[2]));
  BusMux2waybit1 busmux2waybit1_4 (
    .Incrementer(increment[3]), .PC_LOAD(S), .Branch_Address(Branch[3]), .result(result[3]));
endmodule

module PC (
  input  PC_enable,
  input  Carry_in,
  input  [3:0] jump_address,
  input  jump_enb,
  input  clk,
  output [3:0] Q,
  output Carry_out,
  output [3:0] pc_plusone
);

  wire [3:0] busmux2way_1_result;

  reg4bit reg4bit_1 (.enable(PC_enable), .new_data(busmux2way_1_result), .clk(clk), .Q(Q));
  // Incrementer4bit incrementer4bit_1: pin names not known; wires that end beside it: Carry_in, Q, Carry_out, pc_plusone
  // Probe on Q
  BusMux2way busmux2way_1 (.S(jump_enb), .increment(pc_plusone), .Branch(jump_address), .result(busmux2way_1_result));
  // Probe on pc_plusone
endmodule

module memorybank (
  input  enable,
  input  [3:0] W_address,
  input  [7:0] Data,
  output [7:0] Q
);

  wire decoder_1_out0, decoder_1_out1, decoder_1_out2, decoder_1_out3, decoder_1_out4, decoder_1_out5,
       decoder_1_out6, decoder_1_out7, decoder_1_out8, decoder_1_out9, decoder_1_out10, decoder_1_out11,
       decoder_1_out12, decoder_1_out13, decoder_1_out14, decoder_1_out15;
  wire [7:0] reg8bit_1_q, reg8bit_2_q, reg8bit_3_q, reg8bit_4_q, reg8bit_5_q, reg8bit_6_q, reg8bit_7_q,
       reg8bit_8_q, reg8bit_9_q, reg8bit_10_q, reg8bit_11_q, reg8bit_12_q, reg8bit_13_q, reg8bit_14_q,
       reg8bit_15_q, reg8bit_16_q;

  Decoder #(.select(4)) decoder_1 (
    .out0(decoder_1_out0), .out1(decoder_1_out1), .out2(decoder_1_out2), .out3(decoder_1_out3),
    .out4(decoder_1_out4), .out5(decoder_1_out5), .out6(decoder_1_out6), .out7(decoder_1_out7),
    .out8(decoder_1_out8), .out9(decoder_1_out9), .out10(decoder_1_out10), .out11(decoder_1_out11),
    .out12(decoder_1_out12), .out13(decoder_1_out13), .out14(decoder_1_out14), .out15(decoder_1_out15),
    .sel(W_address), .en(enable));
  // Probe on Data
  reg8bit reg8bit_1 (.write(decoder_1_out0), .Data(Data), .Q(reg8bit_1_q));  // open: clk
  reg8bit reg8bit_2 (.write(decoder_1_out1), .Data(Data), .Q(reg8bit_2_q));  // open: clk
  reg8bit reg8bit_3 (.write(decoder_1_out2), .Data(Data), .Q(reg8bit_3_q));  // open: clk
  reg8bit reg8bit_4 (.write(decoder_1_out3), .Data(Data), .Q(reg8bit_4_q));  // open: clk
  reg8bit reg8bit_5 (.write(decoder_1_out4), .Data(Data), .Q(reg8bit_5_q));  // open: clk
  reg8bit reg8bit_6 (.write(decoder_1_out5), .Data(Data), .Q(reg8bit_6_q));  // open: clk
  reg8bit reg8bit_7 (.write(decoder_1_out6), .Data(Data), .Q(reg8bit_7_q));  // open: clk
  reg8bit reg8bit_8 (.write(decoder_1_out7), .Data(Data), .Q(reg8bit_8_q));  // open: clk
  reg8bit reg8bit_9 (.write(decoder_1_out8), .Data(Data), .Q(reg8bit_9_q));  // open: clk
  reg8bit reg8bit_10 (.write(decoder_1_out9), .Data(Data), .Q(reg8bit_10_q));  // open: clk
  reg8bit reg8bit_11 (.write(decoder_1_out10), .Data(Data), .Q(reg8bit_11_q));  // open: clk
  reg8bit reg8bit_12 (.write(decoder_1_out11), .Data(Data), .Q(reg8bit_12_q));  // open: clk
  reg8bit reg8bit_13 (.write(decoder_1_out12), .Data(Data), .Q(reg8bit_13_q));  // open: clk
  reg8bit reg8bit_14 (.write(decoder_1_out13), .Data(Data), .Q(reg8bit_14_q));  // open: clk
  reg8bit reg8bit_15 (.write(decoder_1_out14), .Data(Data), .Q(reg8bit_15_q));  // open: clk
  reg8bit reg8bit_16 (.write(decoder_1_out15), .Data(Data), .Q(reg8bit_16_q));  // open: clk
  Multiplexer #(.select(4), .width(8)) multiplexer_1 (
    .in0(reg8bit_1_q), .in1(reg8bit_2_q), .in2(reg8bit_3_q), .in3(reg8bit_4_q), .in4(reg8bit_5_q),
    .in5(reg8bit_6_q), .in6(reg8bit_7_q), .in7(reg8bit_8_q), .in8(reg8bit_9_q), .in9(reg8bit_10_q),
    .in10(reg8bit_11_q), .in11(reg8bit_12_q), .in12(reg8bit_13_q), .in13(reg8bit_14_q), .in14(reg8bit_15_q),
    .in15(reg8bit_16_q), .out(Q), .sel(W_address));
  // Probe on Q
endmodule

module r_mux (
  input  [7:0] ALU,
  input  [7:0] Mem,
  input  [3:0] IR,
  input  s_alu,
  input  s_mem,
  input  S_ir,
  output [7:0] out_7
);

  wire and_1_out, and_2_out, and_3_out, and_4_out, and_5_out, and_6_out, and_7_out, and_8_out, and_9_out,
       and_10_out, and_11_out, and_12_out, and_13_out, and_14_out, and_15_out, and_16_out, and_17_out,
       and_18_out, and_19_out, and_20_out, and_21_out, and_22_out, and_23_out, and_24_out;

  and and_1 (and_1_out, S_ir, IR[3]);
  and and_2 (and_2_out, S_ir, 1'b0);
  and and_3 (and_3_out, s_mem, Mem[3]);
  and and_4 (and_4_out, s_mem, Mem[7]);
  and and_5 (and_5_out, s_alu, ALU[3]);
  and and_6 (and_6_out, s_alu, ALU[7]);
  or or_1 (out_7[3], and_5_out, and_3_out, and_1_out);
  or or_2 (out_7[7], and_6_out, and_4_out, and_2_out);
  and and_7 (and_7_out, S_ir, IR[2]);
  and and_8 (and_8_out, S_ir, 1'b0);
  and and_9 (and_9_out, s_mem, Mem[6]);
  and and_10 (and_10_out, s_mem, Mem[2]);
  and and_11 (and_11_out, s_alu, ALU[2]);
  or or_3 (out_7[2], and_11_out, and_10_out, and_7_out);
  and and_12 (and_12_out, s_alu, ALU[6]);
  or or_4 (out_7[6], and_12_out, and_9_out, and_8_out);
  and and_13 (and_13_out, S_ir, IR[1]);
  and and_14 (and_14_out, s_mem, Mem[1]);
  and and_15 (and_15_out, S_ir, 1'b0);
  and and_16 (and_16_out, s_mem, Mem[5]);
  and and_17 (and_17_out, s_alu, ALU[1]);
  or or_5 (out_7[1], and_17_out, and_14_out, and_13_out);
  and and_18 (and_18_out, s_alu, ALU[5]);
  and and_19 (and_19_out, S_ir, 1'b0);
  or or_6 (out_7[5], and_18_out, and_16_out, and_15_out);
  and and_20 (and_20_out, s_mem, Mem[0]);
  and and_21 (and_21_out, S_ir, IR[0]);
  and and_22 (and_22_out, s_mem, Mem[4]);
  and and_23 (and_23_out, s_alu, ALU[0]);
  or or_7 (out_7[0], and_23_out, and_20_out, and_21_out);
  and and_24 (and_24_out, s_alu, ALU[4]);
  or or_8 (out_7[4], and_24_out, and_22_out, and_19_out);
endmodule

module control_unit (
  input  [3:0] opcode,
  input  CLK,
  input  fetch,
  input  fetch_w,
  input  execute,
  input  execute_w,
  output add,
  output xor_D,
  output ALU_op_active,
  output AND_D,
  output Halt,
  output R_WRITE,
  output pc_out,
  output Memory_read,
  output IR_w,
  output PC_INCREMENT,
  output ALU_ADD,
  output MAR_WRITE,
  output RS_OUT,
  output ALU_OUT,
  output HALT_WIRE,
  output ALU_XOR,
  output ALU_AND,
  output R_MUX,
  output MEMORY_WRITE,
  output ADDRESS_MUX
);

  wire not_1_out, not_2_out, not_3_out, not_4_out;

  not not_1 (not_1_out, opcode[0]);
  not not_2 (not_2_out, opcode[1]);
  not not_3 (not_3_out, opcode[2]);
  not not_4 (not_4_out, opcode[3]);
  and and_1 (add, not_4_out, not_3_out, not_2_out, not_1_out);
  and and_2 (xor_D, not_4_out, not_3_out, not_2_out, opcode[0]);
  and and_3 (AND_D, not_4_out, not_3_out, opcode[1], not_1_out);
  and and_4 (Halt, not_4_out, not_3_out, opcode[1], opcode[0]);
  or or_1 (ALU_op_active, xor_D, AND_D, add);
  and and_5 (ALU_ADD, execute, add);
  and and_6 (RS_OUT, ALU_op_active, execute);
  and and_7 (ALU_OUT, ALU_op_active, execute);
  and and_8 (R_WRITE, ALU_op_active, execute_w);
  and and_9 (HALT_WIRE, Halt, execute);
  and and_10 (ALU_XOR, execute, xor_D);
  and and_11 (ALU_AND, AND_D, xor_D);

  assign ADDRESS_MUX = 1'b0;
  assign IR_w = fetch_w;
  assign MAR_WRITE = fetch;
  assign Memory_read = fetch;
  assign MEMORY_WRITE = 1'b0;
  assign PC_INCREMENT = fetch_w;
  assign pc_out = fetch;
  assign R_MUX = 1'b0;
endmodule

module CU_16 (
  input  execute,
  input  execute_w,
  input  [3:0] Opcode,
  input  fetch,
  input  fetch_w,
  input  [15:0] R,
  output HALT_detect,
  output ALU_ADD,
  output ALU_SUB,
  output ALU_AND,
  output XOR_detect,
  output ALU_XOR,
  output ALU_L,
  output ALU_R,
  output ALU_B_Mux,
  output Mem0_Addr_Mux_bit0,
  output Mem1_Addr_Mux_bit1,
  output w_memory,
  output RegSrc_bit0,
  output RegSrc_bit1,
  output Reg_Write,
  output PC_OUT,
  output Mem_Read,
  output write_mo,
  output IR_WRITE,
  output Read_Rd_Mux,
  output PC_enable,
  output PC_LOAD,
  output Zero_flag,
  output Positive_flag
);

  wire and_2_out, and_3_out, and_4_out, and_6_out, and_7_out, and_8_out, and_9_out, and_10_out, and_11_out,
       and_12_out, and_13_out, and_14_out, and_15_out, and_16_out, and_18_out, and_19_out, not_1_out,
       not_2_out, not_3_out, not_4_out, not_6_out, not_7_out, or_2_out, or_3_out, or_4_out, or_5_out,
       or_6_out, or_7_out, or_8_out, or_9_out, or_10_out, or_11_out, or_12_out, or_13_out;

  // Probe on Opcode
  not not_1 (not_1_out, Opcode[0]);
  not not_2 (not_2_out, Opcode[1]);
  not not_3 (not_3_out, Opcode[2]);
  not not_4 (not_4_out, Opcode[3]);
  or or_1 (PC_enable, fetch_w, PC_LOAD);
  or or_2 (or_2_out, R[0], R[1], R[2], R[3], R[4], R[5], R[6], R[7], R[9], R[10], R[11], R[12], R[13], R[14], R[15], R[8]);
  not not_5 (Zero_flag, or_2_out);
  not not_6 (not_6_out, Zero_flag);
  not not_7 (not_7_out, R[15]);
  and and_1 (HALT_detect, not_1_out, not_2_out, not_3_out, not_4_out);
  and and_2 (and_2_out, not_4_out, not_3_out, not_2_out, Opcode[0]);
  and and_3 (and_3_out, not_4_out, not_3_out, Opcode[1], not_1_out);
  and and_4 (and_4_out, not_4_out, not_3_out, Opcode[0], Opcode[1]);
  and and_5 (XOR_detect, not_4_out, Opcode[2], not_2_out, not_1_out);
  and and_6 (and_6_out, not_4_out, Opcode[2], not_2_out, Opcode[0]);
  and and_7 (and_7_out, not_4_out, Opcode[2], Opcode[1], not_1_out);
  and and_8 (and_8_out, not_4_out, Opcode[2], Opcode[1], Opcode[0]);
  and and_9 (and_9_out, Opcode[3], not_3_out, not_2_out, not_1_out);
  and and_10 (and_10_out, Opcode[3], not_3_out, not_2_out, Opcode[0]);
  and and_11 (and_11_out, Opcode[3], not_3_out, Opcode[1], not_1_out);
  and and_12 (and_12_out, Opcode[3], not_3_out, Opcode[1], Opcode[0]);
  and and_13 (and_13_out, Opcode[3], Opcode[2], not_2_out, not_1_out);
  and and_14 (and_14_out, Opcode[3], Opcode[2], not_2_out, Opcode[0]);
  and and_15 (and_15_out, Opcode[3], Opcode[2], Opcode[1], not_1_out);
  and and_16 (and_16_out, Opcode[3], Opcode[2], Opcode[1], Opcode[0]);
  and and_17 (Positive_flag, not_6_out, not_7_out);
  or or_3 (or_3_out, and_15_out, and_14_out, and_13_out, and_12_out, and_10_out);
  or or_4 (or_4_out, and_16_out, and_11_out, and_9_out, and_8_out, and_7_out, and_6_out, XOR_detect, and_4_out, and_3_out, and_2_out);
  and and_18 (and_18_out, and_13_out, Zero_flag);
  and and_19 (and_19_out, and_14_out, Positive_flag);
  or or_5 (or_5_out, and_18_out, and_16_out, and_15_out, and_19_out);
  and and_20 (ALU_ADD, execute, and_2_out);
  and and_21 (ALU_SUB, execute, and_3_out);
  and and_22 (ALU_AND, execute, and_4_out);
  and and_23 (ALU_XOR, execute, XOR_detect);
  and and_24 (ALU_L, execute, and_6_out);
  and and_25 (ALU_R, execute, and_7_out);
  or or_6 (or_6_out, and_9_out, and_10_out);
  or or_7 (or_7_out, and_8_out, and_9_out, and_10_out);
  or or_8 (or_8_out, and_11_out, and_12_out);
  or or_9 (or_9_out, and_10_out, and_12_out);
  or or_10 (or_10_out, and_9_out, and_11_out);
  or or_11 (or_11_out, and_8_out, and_16_out);
  or or_12 (or_12_out, execute, execute_w);
  and and_26 (ALU_B_Mux, execute, or_6_out);
  or or_13 (or_13_out, execute, execute_w);
  and and_27 (Mem1_Addr_Mux_bit1, or_13_out, or_8_out);
  and and_28 (w_memory, execute_w, or_9_out);
  and and_29 (RegSrc_bit0, execute_w, or_10_out);
  and and_30 (RegSrc_bit1, execute_w, or_11_out);
  and and_31 (Reg_Write, execute_w, or_4_out);
  and and_32 (Read_Rd_Mux, or_12_out, or_3_out);
  and and_33 (PC_LOAD, execute_w, or_5_out);
  and and_34 (Mem0_Addr_Mux_bit0, or_13_out, or_7_out);

  assign IR_WRITE = fetch_w;
  assign Mem_Read = fetch;
  assign PC_OUT = fetch;
  assign write_mo = fetch;
endmodule

module Final_milston2 (
  input  RUN,
  input  in_2,
  input  [3:0] opcode
);

  wire clock_control_1_execute_w, clock_control_1_fetch, clock_control_1_fetch_w, not_1_out, pc_1_p1,
       undriven, undriven_2, undriven_3;
  wire [3:0] busmux2way_1_result, IR_q, pc_1_p4;
  wire [7:0] final_1_out_9, MEMORY_q, r_mux_1_out_7, R_q;

  not not_1 (not_1_out, in_2);
  clock_control clock_control_1 (
    .RUN(RUN), .halt(not_1_out), .fetch(clock_control_1_fetch), .fetch_w(clock_control_1_fetch_w),
    .execute_w(clock_control_1_execute_w));  // open: Cl, execute
  FINAL final_1 (.A(R_q), .out_9(final_1_out_9));  // open: B, ADD, SUB, XOR_r, AND_r, R_shift_r, L_shift_l
  r_mux r_mux_1 (
    .ALU(final_1_out_9), .Mem(MEMORY_q), .IR(IR_q), .s_alu(undriven), .s_mem(undriven_2), .S_ir(undriven_3),
    .out_7(r_mux_1_out_7));
  reg8bit R (.Data(r_mux_1_out_7), .Q(R_q));  // open: write, clk
  reg8bit IR (.write(clock_control_1_fetch_w), .Data(MEMORY_q), .Q({opcode, IR_q}));  // open: clk
  // PC pc_1: pin names not known; wires that end beside it: pc_1_p1, IR_q, clock_control_1_execute_w, pc_1_p4, pc_1_p4
  BusMux2way busmux2way_1 (.S(clock_control_1_fetch), .increment(IR_q), .Branch(pc_1_p4), .result(busmux2way_1_result));
  memorybank MEMORY (.W_address(busmux2way_1_result), .Data(R_q), .Q(MEMORY_q));  // open: enable
endmodule

module Adder_16 (
  input  carry_in,
  input  [15:0] A,
  input  [15:0] B,
  output [15:0] sum,
  output carrry_out
);

  wire adder_8_bit_1_carry_out;

  // Probe on A
  // Probe on B
  ADDER_8_BIT adder_8_bit_1 (
    .A(A[7:0]), .carry(carry_in), .B(B[7:0]), .SUM(sum[7:0]), .Carry_out(adder_8_bit_1_carry_out));
  ADDER_8_BIT adder_8_bit_2 (
    .A(A[15:8]), .carry(adder_8_bit_1_carry_out), .B(B[15:8]), .SUM(sum[15:8]), .Carry_out(carrry_out));
  // Probe on sum
endmodule

module Sub_16 (
  input  [15:0] A,
  input  [15:0] B,
  output [15:0] sub,
  output cRRY_OUT
);

  wire sub_8_1_borrow;

  // Probe on A
  // Probe on B
  sub_8 sub_8_1 (.A(A[7:0]), .carry_in(1'b1), .B(B[7:0]), .result(sub[7:0]), .borrow(sub_8_1_borrow));
  sub_8 sub_8_2 (.A(A[15:8]), .carry_in(sub_8_1_borrow), .B(B[15:8]), .result(sub[15:8]), .borrow(cRRY_OUT));
  // Probe on sub
endmodule

module XOR_16 (
  input  [15:0] A,
  input  [15:0] B,
  output [15:0] xor_result
);

  // Probe on A
  // Probe on B
  XOR_8BIT xor_8bit_1 (.A(A[7:0]), .B(B[7:0]), .result(xor_result[7:0]));
  XOR_8BIT xor_8bit_2 (.A(A[15:8]), .B(B[15:8]), .result(xor_result[15:8]));
  // Probe on xor_result
endmodule

module AND_16 (
  input  [15:0] A,
  input  [15:0] B,
  output [15:0] AND_result
);

  // Probe on A
  // Probe on B
  AND_8BIT and_8bit_1 (.A(A[7:0]), .B(B[7:0]), .result(AND_result[7:0]));
  AND_8BIT and_8bit_2 (.A(A[15:8]), .B(B[15:8]), .result(AND_result[15:8]));
  // Probe on AND_result
endmodule

module L_SHIFT_16 (
  input  [15:0] A,
  output [15:0] shift_L
);

  wire l_shift_1_carry_out;

  l_shift l_shift_1 (.carry_in(1'b0), .A(A[7:0]), .carry_Out(l_shift_1_carry_out), .result(shift_L[7:0]));
  l_shift l_shift_2 (.carry_in(l_shift_1_carry_out), .A(A[15:8]), .result(shift_L[15:8]));  // open: carry_Out
endmodule

module R_SHIFT_16 (
  input  [15:0] A,
  output [15:0] Shift_R
);

  wire r_shift_2_carry_out;

  R_shift r_shift_1 (.A(A[7:0]), .Carry_in(r_shift_2_carry_out), .result(Shift_R[7:0]));  // open: carry_out
  R_shift r_shift_2 (.A(A[15:8]), .Carry_in(1'b0), .carry_out(r_shift_2_carry_out), .result(Shift_R[15:8]));
endmodule

module Hotmux_16 (
  input  sel_add,
  input  sel_sub,
  input  sel_xor,
  input  sel_and,
  input  sel_r,
  input  sel_l,
  input  [15:0] ADD,
  input  [15:0] SUB,
  input  [15:0] XOR_in,
  input  [15:0] AND_IN,
  input  [15:0] R_shift,
  input  [15:0] L_shift,
  output [15:0] result
);

  hot_8_mux hot_8_mux_1 (
    .sel_add(sel_add), .sel_sub(sel_sub), .sel_xor(sel_xor), .sel_and(sel_and), .sel_Rshift(sel_r),
    .sel_Lshift(sel_l), .add(ADD[7:0]), .l_shift(L_shift[7:0]), .and_b(AND_IN[7:0]), .r_shift(R_shift[7:0]),
    .sub(SUB[7:0]), .xor_in(XOR_in[7:0]), .resul(result[7:0]));
  hot_8_mux hot_8_mux_2 (
    .sel_add(sel_add), .sel_sub(sel_sub), .sel_xor(sel_xor), .sel_and(sel_and), .sel_Rshift(sel_r),
    .sel_Lshift(sel_l), .add(ADD[15:8]), .l_shift(L_shift[15:8]), .and_b(AND_IN[15:8]),
    .r_shift(R_shift[15:8]), .sub(SUB[15:8]), .xor_in(XOR_in[15:8]), .resul(result[15:8]));
endmodule

module Write_Back_Vault (
  input  clock,
  input  [15:0] Data,
  input  w_enable,
  input  reset,
  output [15:0] Data_out
);

  Register #(.width(16)) register_1 (.D(Data), .en(w_enable), .clk(clock), .Q(Data_out), .clr(reset));
endmodule

module Amux_1bit (
  input  A,
  input  B,
  input  C,
  input  S0,
  input  S1,
  output out_6
);

  wire and_1_out, and_2_out, and_3_out, and_4_out, and_5_out, and_6_out, not_1_out, not_2_out;

  not not_1 (not_1_out, S0);
  not not_2 (not_2_out, S1);
  and and_1 (and_1_out, not_1_out, not_2_out);
  and and_2 (and_2_out, not_2_out, S0);
  and and_3 (and_3_out, S1, not_1_out);
  and and_4 (and_4_out, A, and_1_out);
  and and_5 (and_5_out, B, and_2_out);
  and and_6 (and_6_out, C, and_3_out);
  or or_1 (out_6, and_4_out, and_5_out, and_6_out);
endmodule

module Amux_8bit (
  input  [7:0] A,
  input  [7:0] B,
  input  [7:0] c,
  input  [1:0] s,
  output [7:0] result
);

  // Probe on B
  Amux_1bit amux_1bit_1 (.A(A[0]), .B(B[0]), .C(c[0]), .S0(s[0]), .S1(s[1]), .out_6(result[0]));
  Amux_1bit amux_1bit_2 (.A(A[1]), .B(B[1]), .C(c[1]), .S0(s[0]), .S1(s[1]), .out_6(result[1]));
  Amux_1bit amux_1bit_3 (.A(A[2]), .B(B[2]), .C(c[2]), .S0(s[0]), .S1(s[1]), .out_6(result[2]));
  Amux_1bit amux_1bit_4 (.A(A[3]), .B(B[3]), .C(c[3]), .S0(s[0]), .S1(s[1]), .out_6(result[3]));
  Amux_1bit amux_1bit_5 (.A(A[4]), .B(B[4]), .C(c[4]), .S0(s[0]), .S1(s[1]), .out_6(result[4]));
  Amux_1bit amux_1bit_6 (.A(A[5]), .B(B[5]), .C(c[5]), .S0(s[0]), .S1(s[1]), .out_6(result[5]));
  Amux_1bit amux_1bit_7 (.A(A[6]), .B(B[6]), .C(c[6]), .S0(s[0]), .S1(s[1]), .out_6(result[6]));
  Amux_1bit amux_1bit_8 (.A(A[7]), .B(B[7]), .C(c[7]), .S0(s[0]), .S1(s[1]), .out_6(result[7]));
  // Probe on result
endmodule

module Final_CPU (
);

  wire alu_16bit_1_postive, alu_16bit_1_zero, clock_1_out, clock_2_out, pc_16_1_p1, pc_16_1_p2,
       phase_generator16_1_p2, phase_generator16_1_p3, phase_generator16_1_p4, phase_generator16_1_p5,
       undriven_2, undriven_3, undriven_4, undriven_6, undriven_7, undriven_8, undriven_9, undriven_10,
       undriven_11, undriven_12;
  wire [1:0] undriven, undriven_5;
  wire [3:0] ir_regi16bit_1_d, ir_regi16bit_1_opcode, ir_regi16bit_1_s, ir_regi16bit_1_t;
  wire [7:0] amux_8bit_1_result, ir_regi16bit_1_addr, multiplexer_1_out, pc_16_1_p5, pc_16_1_p6,
       registerfile_16_1_rt_data, registerfile_16_1_rt_data_2;
  wire [15:0] alu_16bit_1_result, memory_16_1_data_out, multiplexer_2_out, r_mux16_1_result, register_1_q,
       registerfile_16_1_rs_data;

  Clock clock_1 (.out(clock_1_out));
  Clock clock_2 (.out(clock_2_out));
  Multiplexer #(.width(8)) multiplexer_1 (
    .in0(ir_regi16bit_1_addr), .in1(registerfile_16_1_rt_data), .out(multiplexer_1_out), .sel(undriven_6));
  // phase_generator16 phase_generator16_1: pin names not known; wires that end beside it: clock_1_out, phase_generator16_1_p2, phase_generator16_1_p3, phase_generator16_1_p4, phase_generator16_1_p5
  // PC_16 pc_16_1: pin names not known; wires that end beside it: pc_16_1_p1, pc_16_1_p2, multiplexer_1_out, clock_2_out, pc_16_1_p5, pc_16_1_p6
  Amux_8bit amux_8bit_1 (
    .A(pc_16_1_p5), .B(ir_regi16bit_1_addr), .c(registerfile_16_1_rs_data[7:0]), .s(undriven),
    .result(amux_8bit_1_result));
  Multiplexer #(.width(16)) multiplexer_2 (
    .in0(r_mux16_1_result), .in1({{8{1'b0}}, ir_regi16bit_1_addr}), .out(multiplexer_2_out), .sel(undriven_3));
  memory_16 memory_16_1 (
    .w_enable(undriven_2), .Address(amux_8bit_1_result), .CLK(clock_2_out),
    .Data_in({registerfile_16_1_rt_data_2, registerfile_16_1_rt_data}), .Data_out(memory_16_1_data_out));  // open: in_5
  // Probe on multiplexer_2_out
  Register #(.width(16)) register_1 (
    .D(multiplexer_2_out), .en(1'b1), .clk(phase_generator16_1_p5), .Q(register_1_q));  // open: clr
  IR_regi16bit ir_regi16bit_1 (
    .write(phase_generator16_1_p3), .Data(memory_16_1_data_out), .clk(clock_2_out),
    .OPCODE(ir_regi16bit_1_opcode), .d(ir_regi16bit_1_d), .S(ir_regi16bit_1_s), .T(ir_regi16bit_1_t),
    .addr(ir_regi16bit_1_addr));
  registerfile_16 registerfile_16_1 (
    .clk(clock_2_out), .rs_addr(ir_regi16bit_1_s), .rt_addr(ir_regi16bit_1_t), .rd_addr(ir_regi16bit_1_d),
    .data(register_1_q), .reg_write(undriven_4), .Read_Rd_Mux(undriven_6),
    .rs_data(registerfile_16_1_rs_data), .rt_data({registerfile_16_1_rt_data_2, registerfile_16_1_rt_data}));
  R_mux16 r_mux16_1 (
    .ALU(alu_16bit_1_result), .MEM(memory_16_1_data_out), .pc_incre({{8{1'b0}}, pc_16_1_p6}), .s(undriven_5),
    .result(r_mux16_1_result));
  // decorder decorder_1: pin names not known; wires that end beside it: phase_generator16_1_p2, phase_generator16_1_p3, pc_16_1_p1
  ALU_16bit alu_16bit_1 (
    .A(registerfile_16_1_rs_data), .B({registerfile_16_1_rt_data_2, registerfile_16_1_rt_data}),
    .sel_add(undriven_7), .sel_sub(undriven_8), .sel_xor(undriven_10), .sel_and(undriven_9),
    .sel_r(undriven_12), .sel_l(undriven_11), .result(alu_16bit_1_result), .zero(alu_16bit_1_zero),
    .postive(alu_16bit_1_postive));  // open: B_pass
endmodule

module R_mux16 (
  input  [15:0] ALU,
  input  [15:0] MEM,
  input  [15:0] pc_incre,
  input  [1:0] s,
  output [15:0] result
);

  // Probe on s
  Amux_8bit amux_8bit_1 (.A(ALU[7:0]), .B(MEM[7:0]), .c(pc_incre[7:0]), .s(s), .result(result[7:0]));
  Amux_8bit amux_8bit_2 (.A(ALU[15:8]), .B(MEM[15:8]), .c(pc_incre[15:8]), .s(s), .result(result[15:8]));
endmodule

module IR_regi16bit (
  input  write,
  input  [15:0] Data,
  input  clk,
  output [3:0] OPCODE,
  output [3:0] d,
  output [3:0] S,
  output [3:0] T,
  output [7:0] addr
);

  reg8bit reg8bit_1 (.write(write), .Data(Data[7:0]), .clk(clk), .Q(addr));
  reg8bit reg8bit_2 (.write(write), .Data(Data[15:8]), .clk(clk), .Q({OPCODE, d}));
  // Probe on addr[3:0]
  // Probe on addr

  assign S = addr[7:4];
  assign T = addr[3:0];
endmodule

module CPU_16BIT_TOY (
);

  wire amux_8bit_2_p4, amux_8bit_2_p5, clock_1_out, cu_16_1_p7, cu_16_1_p8, cu_16_1_p9, cu_16_1_p10,
       cu_16_1_p11, cu_16_1_p12, cu_16_1_p15, phase_generator16_1_execute, phase_generator16_1_execute_w,
       phase_generator16_1_fetch, phase_generator16_1_fetch_w, undriven, undriven_3, undriven_4, undriven_5,
       undriven_6;
  wire [1:0] cu_16_1_p16, undriven_2;
  wire [7:0] amux_8bit_1_result, amux_8bit_2_p3, amux_8bit_2_p6, amux_8bit_3_result, amux_8bit_4_result,
       memory_16_1_data_out, memory_16_1_data_out_2, pc_16_1_q, registerfile_16_1_rt_data;
  wire [15:0] alu_16bit_1_result, register_1_q, registerfile_16_1_rs_data, write_back_vault_1_data_out;

  Clock clock_1 (.out(clock_1_out));
  phase_generator16 phase_generator16_1 (
    .CLK(clock_1_out), .halt(clock_1_out), .Fetch(phase_generator16_1_fetch),
    .fetch_w(phase_generator16_1_fetch_w), .execute(phase_generator16_1_execute),
    .execute_w(phase_generator16_1_execute_w));
  PC_16 pc_16_1 (
    .pc_enable(undriven_3), .load(undriven), .Jump_add(amux_8bit_1_result), .clk(clock_1_out), .Q(pc_16_1_q));
  Amux_8bit amux_8bit_1 (
    .A(register_1_q[7:0]), .B(amux_8bit_2_p3), .c({8{1'b0}}), .s(undriven_2), .result(amux_8bit_1_result));
  // Probe on {memory_16_1_data_out_2, memory_16_1_data_out}
  memory_16 memory_16_1 (
    .w_enable(cu_16_1_p15), .Address(amux_8bit_2_p6), .CLK(clock_1_out),
    .Data_in({registerfile_16_1_rt_data, amux_8bit_2_p3}),
    .Data_out({memory_16_1_data_out_2, memory_16_1_data_out}));  // open: in_5
  // Amux_8bit amux_8bit_2: pin names not known; wires that end beside it: pc_16_1_q, register_1_q[7:0], amux_8bit_2_p3, amux_8bit_2_p4, amux_8bit_2_p5, amux_8bit_2_p6
  Amux_8bit amux_8bit_3 (
    .A(write_back_vault_1_data_out[15:8]), .B(memory_16_1_data_out_2), .c({8{1'b0}}), .s(cu_16_1_p16),
    .result(amux_8bit_3_result));
  Amux_8bit amux_8bit_4 (
    .A(write_back_vault_1_data_out[7:0]), .B(memory_16_1_data_out), .c(register_1_q[7:0]), .s(cu_16_1_p16),
    .result(amux_8bit_4_result));
  Register #(.width(16)) register_1 (
    .D({memory_16_1_data_out_2, memory_16_1_data_out}), .en(undriven_4), .clk(clock_1_out), .Q(register_1_q));  // open: clr
  // Probe on {amux_8bit_3_result, amux_8bit_4_result}
  registerfile_16 registerfile_16_1 (
    .clk(clock_1_out), .rs_addr(register_1_q[7:4]), .rt_addr(register_1_q[3:0]),
    .rd_addr(register_1_q[11:8]), .data({amux_8bit_3_result, amux_8bit_4_result}), .reg_write(undriven_5),
    .Read_Rd_Mux(undriven_6), .rs_data(registerfile_16_1_rs_data),
    .rt_data({registerfile_16_1_rt_data, amux_8bit_2_p3}));
  Write_Back_Vault write_back_vault_1 (
    .clock(clock_1_out), .Data(alu_16bit_1_result), .w_enable(phase_generator16_1_execute),
    .Data_out(write_back_vault_1_data_out));  // open: reset
  // CU_16 cu_16_1: pin names not known; wires that end beside it: phase_generator16_1_execute, phase_generator16_1_execute_w, register_1_q[15:12], phase_generator16_1_fetch, phase_generator16_1_fetch_w, {registerfile_16_1_rt_data, amux_8bit_2_p3}, cu_16_1_p7, cu_16_1_p8, cu_16_1_p9, cu_16_1_p10, cu_16_1_p11, cu_16_1_p12, amux_8bit_2_p4, amux_8bit_2_p5, cu_16_1_p15, cu_16_1_p16
  ALU_16bit alu_16bit_1 (
    .A(registerfile_16_1_rs_data), .B({registerfile_16_1_rt_data, amux_8bit_2_p3}), .sel_add(cu_16_1_p7),
    .sel_sub(cu_16_1_p8), .sel_xor(cu_16_1_p10), .sel_and(cu_16_1_p9), .sel_r(cu_16_1_p12),
    .sel_l(cu_16_1_p11), .result(alu_16bit_1_result));  // open: B_pass, zero, postive
endmodule

module decorder (
  input  [3:0] Opcode,
  output [15:0] result
);

  wire not_1_out, not_2_out, not_3_out, not_4_out;

  not not_1 (not_1_out, Opcode[0]);
  not not_2 (not_2_out, Opcode[1]);
  not not_3 (not_3_out, Opcode[2]);
  not not_4 (not_4_out, Opcode[3]);
  and ADD (result[1], Opcode[0], not_2_out, not_3_out, not_4_out);
  and SUB (result[2], not_4_out, not_3_out, Opcode[1], not_1_out);
  and AND_D (result[3], not_4_out, not_3_out, Opcode[1], Opcode[0]);
  and XOR_d (result[4], not_4_out, Opcode[2], not_2_out, not_1_out);
  and LSH (result[5], not_4_out, Opcode[2], not_2_out, Opcode[0]);
  and RSH (result[6], not_4_out, Opcode[2], Opcode[1], not_1_out);
  and and_1 (result[7], not_4_out, Opcode[2], Opcode[1], Opcode[0]);
  and and_2 (result[8], Opcode[3], not_3_out, not_2_out, not_1_out);
  and and_3 (result[9], Opcode[3], not_3_out, not_2_out, Opcode[0]);
  and and_4 (result[10], Opcode[3], not_3_out, Opcode[1], not_1_out);
  and and_5 (result[11], Opcode[3], not_3_out, Opcode[1], Opcode[0]);
  and and_6 (result[12], Opcode[3], Opcode[2], not_2_out, not_1_out);
  and and_7 (result[13], Opcode[3], Opcode[2], not_2_out, Opcode[0]);
  and and_8 (result[14], Opcode[3], Opcode[2], Opcode[1], not_1_out);
  and and_9 (result[15], Opcode[3], Opcode[2], Opcode[1], Opcode[0]);
  and Halt (result[0], not_1_out, not_2_out, not_3_out, not_4_out);

  // Notes on the sheet:
  //   load adder
  //   load
  //   store
  //   load_indirect
  //   store_indirect
  //   branch_0
  //   branch_+
  //   jump_reg
  //   jumo_AND_link
endmodule

module rshift_16 (
  input  [15:0] A,
  input  [15:0] B,
  output [15:0] result
);

  wire multiplexer_1_out, multiplexer_2_out, multiplexer_3_out, multiplexer_4_out, multiplexer_5_out,
       multiplexer_6_out, multiplexer_7_out, multiplexer_8_out, multiplexer_9_out, multiplexer_10_out,
       multiplexer_11_out, multiplexer_12_out, multiplexer_13_out, multiplexer_14_out, multiplexer_15_out,
       multiplexer_16_out, multiplexer_17_out, multiplexer_18_out, multiplexer_19_out, multiplexer_20_out,
       multiplexer_21_out, multiplexer_22_out, multiplexer_23_out, multiplexer_24_out, multiplexer_25_out,
       multiplexer_26_out, multiplexer_27_out, multiplexer_28_out, multiplexer_29_out, multiplexer_30_out,
       multiplexer_31_out, multiplexer_32_out, multiplexer_33_out, multiplexer_34_out, multiplexer_35_out,
       multiplexer_36_out, multiplexer_37_out, multiplexer_38_out, multiplexer_39_out, multiplexer_40_out,
       multiplexer_41_out, multiplexer_42_out, multiplexer_43_out, multiplexer_44_out, multiplexer_45_out,
       multiplexer_46_out, multiplexer_47_out, multiplexer_48_out;

  Multiplexer multiplexer_1 (.in0(A[0]), .in1(A[1]), .out(multiplexer_1_out), .sel(B[0]));
  Multiplexer multiplexer_2 (.in0(A[1]), .in1(A[2]), .out(multiplexer_2_out), .sel(B[0]));
  Multiplexer multiplexer_3 (.in0(A[2]), .in1(A[3]), .out(multiplexer_3_out), .sel(B[0]));
  Multiplexer multiplexer_4 (.in0(A[3]), .in1(A[4]), .out(multiplexer_4_out), .sel(B[0]));
  Multiplexer multiplexer_5 (.in0(A[4]), .in1(A[5]), .out(multiplexer_5_out), .sel(B[0]));
  Multiplexer multiplexer_6 (.in0(A[5]), .in1(A[6]), .out(multiplexer_6_out), .sel(B[0]));
  Multiplexer multiplexer_7 (.in0(A[6]), .in1(A[7]), .out(multiplexer_7_out), .sel(B[0]));
  Multiplexer multiplexer_8 (.in0(A[7]), .in1(A[8]), .out(multiplexer_8_out), .sel(B[0]));
  Multiplexer multiplexer_9 (.in0(A[8]), .in1(A[9]), .out(multiplexer_9_out), .sel(B[0]));
  Multiplexer multiplexer_10 (.in0(A[9]), .in1(A[10]), .out(multiplexer_10_out), .sel(B[0]));
  Multiplexer multiplexer_11 (.in0(A[10]), .in1(A[11]), .out(multiplexer_11_out), .sel(B[0]));
  Multiplexer multiplexer_12 (.in0(A[11]), .in1(A[12]), .out(multiplexer_12_out), .sel(B[0]));
  Multiplexer multiplexer_13 (.in0(A[12]), .in1(A[13]), .out(multiplexer_13_out), .sel(B[0]));
  Multiplexer multiplexer_14 (.in0(A[13]), .in1(A[14]), .out(multiplexer_14_out), .sel(B[0]));
  Multiplexer multiplexer_15 (.in0(A[14]), .in1(A[15]), .out(multiplexer_15_out), .sel(B[0]));
  Multiplexer multiplexer_16 (.in0(A[15]), .in1(1'b0), .out(multiplexer_16_out), .sel(B[0]));
  Multiplexer multiplexer_17 (.in0(multiplexer_1_out), .in1(multiplexer_3_out), .out(multiplexer_17_out), .sel(B[1]));
  Multiplexer multiplexer_18 (.in0(multiplexer_2_out), .in1(multiplexer_4_out), .out(multiplexer_18_out), .sel(B[1]));
  Multiplexer multiplexer_19 (.in0(multiplexer_3_out), .in1(multiplexer_5_out), .out(multiplexer_19_out), .sel(B[1]));
  Multiplexer multiplexer_20 (.in0(multiplexer_4_out), .in1(multiplexer_6_out), .out(multiplexer_20_out), .sel(B[1]));
  Multiplexer multiplexer_21 (.in0(multiplexer_5_out), .in1(multiplexer_7_out), .out(multiplexer_21_out), .sel(B[1]));
  Multiplexer multiplexer_22 (.in0(multiplexer_6_out), .in1(multiplexer_8_out), .out(multiplexer_22_out), .sel(B[1]));
  Multiplexer multiplexer_23 (.in0(multiplexer_7_out), .in1(multiplexer_9_out), .out(multiplexer_23_out), .sel(B[1]));
  Multiplexer multiplexer_24 (.in0(multiplexer_8_out), .in1(multiplexer_10_out), .out(multiplexer_24_out), .sel(B[1]));
  Multiplexer multiplexer_25 (.in0(multiplexer_9_out), .in1(multiplexer_11_out), .out(multiplexer_25_out), .sel(B[1]));
  Multiplexer multiplexer_26 (.in0(multiplexer_10_out), .in1(multiplexer_12_out), .out(multiplexer_26_out), .sel(B[1]));
  Multiplexer multiplexer_27 (.in0(multiplexer_11_out), .in1(multiplexer_13_out), .out(multiplexer_27_out), .sel(B[1]));
  Multiplexer multiplexer_28 (.in0(multiplexer_12_out), .in1(multiplexer_14_out), .out(multiplexer_28_out), .sel(B[1]));
  Multiplexer multiplexer_29 (.in0(multiplexer_13_out), .in1(multiplexer_15_out), .out(multiplexer_29_out), .sel(B[1]));
  Multiplexer multiplexer_30 (.in0(multiplexer_14_out), .in1(multiplexer_16_out), .out(multiplexer_30_out), .sel(B[1]));
  Multiplexer multiplexer_31 (.in0(multiplexer_15_out), .in1(1'b0), .out(multiplexer_31_out), .sel(B[1]));
  Multiplexer multiplexer_32 (.in0(multiplexer_16_out), .in1(1'b0), .out(multiplexer_32_out), .sel(B[1]));
  Multiplexer multiplexer_33 (.in0(multiplexer_17_out), .in1(multiplexer_21_out), .out(multiplexer_33_out), .sel(B[2]));
  Multiplexer multiplexer_34 (.in0(multiplexer_18_out), .in1(multiplexer_22_out), .out(multiplexer_34_out), .sel(B[2]));
  Multiplexer multiplexer_35 (.in0(multiplexer_19_out), .in1(multiplexer_23_out), .out(multiplexer_35_out), .sel(B[2]));
  Multiplexer multiplexer_36 (.in0(multiplexer_20_out), .in1(multiplexer_24_out), .out(multiplexer_36_out), .sel(B[2]));
  Multiplexer multiplexer_37 (.in0(multiplexer_21_out), .in1(multiplexer_25_out), .out(multiplexer_37_out), .sel(B[2]));
  Multiplexer multiplexer_38 (.in0(multiplexer_22_out), .in1(multiplexer_26_out), .out(multiplexer_38_out), .sel(B[2]));
  Multiplexer multiplexer_39 (.in0(multiplexer_23_out), .in1(multiplexer_27_out), .out(multiplexer_39_out), .sel(B[2]));
  Multiplexer multiplexer_40 (.in0(multiplexer_24_out), .in1(multiplexer_28_out), .out(multiplexer_40_out), .sel(B[2]));
  Multiplexer multiplexer_41 (.in0(multiplexer_25_out), .in1(multiplexer_29_out), .out(multiplexer_41_out), .sel(B[2]));
  Multiplexer multiplexer_42 (.in0(multiplexer_26_out), .in1(multiplexer_30_out), .out(multiplexer_42_out), .sel(B[2]));
  Multiplexer multiplexer_43 (.in0(multiplexer_27_out), .in1(multiplexer_31_out), .out(multiplexer_43_out), .sel(B[2]));
  Multiplexer multiplexer_44 (.in0(multiplexer_28_out), .in1(multiplexer_32_out), .out(multiplexer_44_out), .sel(B[2]));
  Multiplexer multiplexer_45 (.in0(multiplexer_29_out), .in1(1'b0), .out(multiplexer_45_out), .sel(B[2]));
  Multiplexer multiplexer_46 (.in0(multiplexer_30_out), .in1(1'b0), .out(multiplexer_46_out), .sel(B[2]));
  Multiplexer multiplexer_47 (.in0(multiplexer_31_out), .in1(1'b0), .out(multiplexer_47_out), .sel(B[2]));
  Multiplexer multiplexer_48 (.in0(multiplexer_32_out), .in1(1'b0), .out(multiplexer_48_out), .sel(B[2]));
  Multiplexer multiplexer_49 (.in0(multiplexer_33_out), .in1(multiplexer_41_out), .out(result[0]), .sel(B[3]));
  Multiplexer multiplexer_50 (.in0(multiplexer_34_out), .in1(multiplexer_42_out), .out(result[1]), .sel(B[3]));
  Multiplexer multiplexer_51 (.in0(multiplexer_35_out), .in1(multiplexer_43_out), .out(result[2]), .sel(B[3]));
  Multiplexer multiplexer_52 (.in0(multiplexer_36_out), .in1(multiplexer_44_out), .out(result[3]), .sel(B[3]));
  Multiplexer multiplexer_53 (.in0(multiplexer_37_out), .in1(multiplexer_45_out), .out(result[4]), .sel(B[3]));
  Multiplexer multiplexer_54 (.in0(multiplexer_38_out), .in1(multiplexer_46_out), .out(result[5]), .sel(B[3]));
  Multiplexer multiplexer_55 (.in0(multiplexer_39_out), .in1(multiplexer_47_out), .out(result[6]), .sel(B[3]));
  Multiplexer multiplexer_56 (.in0(multiplexer_40_out), .in1(multiplexer_48_out), .out(result[7]), .sel(B[3]));
  Multiplexer multiplexer_57 (.in0(multiplexer_41_out), .in1(1'b0), .out(result[8]), .sel(B[3]));
  Multiplexer multiplexer_58 (.in0(multiplexer_42_out), .in1(1'b0), .out(result[9]), .sel(B[3]));
  Multiplexer multiplexer_59 (.in0(multiplexer_43_out), .in1(1'b0), .out(result[10]), .sel(B[3]));
  Multiplexer multiplexer_60 (.in0(multiplexer_44_out), .in1(1'b0), .out(result[11]), .sel(B[3]));
  Multiplexer multiplexer_61 (.in0(multiplexer_45_out), .in1(1'b0), .out(result[12]), .sel(B[3]));
  Multiplexer multiplexer_62 (.in0(multiplexer_46_out), .in1(1'b0), .out(result[13]), .sel(B[3]));
  Multiplexer multiplexer_63 (.in0(multiplexer_47_out), .in1(1'b0), .out(result[14]), .sel(B[3]));
  Multiplexer multiplexer_64 (.in0(multiplexer_48_out), .in1(1'b0), .out(result[15]), .sel(B[3]));
endmodule

module Lshift_16 (
  input  [15:0] A,
  input  [15:0] B,
  output [15:0] result
);

  wire multiplexer_1_out, multiplexer_2_out, multiplexer_3_out, multiplexer_4_out, multiplexer_5_out,
       multiplexer_6_out, multiplexer_7_out, multiplexer_8_out, multiplexer_9_out, multiplexer_10_out,
       multiplexer_11_out, multiplexer_12_out, multiplexer_13_out, multiplexer_14_out, multiplexer_15_out,
       multiplexer_16_out, multiplexer_17_out, multiplexer_18_out, multiplexer_19_out, multiplexer_20_out,
       multiplexer_21_out, multiplexer_22_out, multiplexer_23_out, multiplexer_24_out, multiplexer_25_out,
       multiplexer_26_out, multiplexer_27_out, multiplexer_28_out, multiplexer_29_out, multiplexer_30_out,
       multiplexer_31_out, multiplexer_32_out, multiplexer_33_out, multiplexer_34_out, multiplexer_35_out,
       multiplexer_36_out, multiplexer_37_out, multiplexer_38_out, multiplexer_39_out, multiplexer_40_out,
       multiplexer_41_out, multiplexer_42_out, multiplexer_43_out, multiplexer_44_out, multiplexer_45_out,
       multiplexer_46_out, multiplexer_47_out, multiplexer_48_out;

  Multiplexer multiplexer_1 (.in0(A[0]), .in1(1'b0), .out(multiplexer_1_out), .sel(B[0]));
  Multiplexer multiplexer_2 (.in0(A[1]), .in1(A[0]), .out(multiplexer_2_out), .sel(B[0]));
  Multiplexer multiplexer_3 (.in0(A[2]), .in1(A[1]), .out(multiplexer_3_out), .sel(B[0]));
  Multiplexer multiplexer_4 (.in0(A[3]), .in1(A[2]), .out(multiplexer_4_out), .sel(B[0]));
  Multiplexer multiplexer_5 (.in0(A[4]), .in1(A[3]), .out(multiplexer_5_out), .sel(B[0]));
  Multiplexer multiplexer_6 (.in0(A[5]), .in1(A[4]), .out(multiplexer_6_out), .sel(B[0]));
  Multiplexer multiplexer_7 (.in0(A[6]), .in1(A[5]), .out(multiplexer_7_out), .sel(B[0]));
  Multiplexer multiplexer_8 (.in0(A[7]), .in1(A[6]), .out(multiplexer_8_out), .sel(B[0]));
  Multiplexer multiplexer_9 (.in0(A[8]), .in1(A[7]), .out(multiplexer_9_out), .sel(B[0]));
  Multiplexer multiplexer_10 (.in0(A[9]), .in1(A[8]), .out(multiplexer_10_out), .sel(B[0]));
  Multiplexer multiplexer_11 (.in0(A[10]), .in1(A[9]), .out(multiplexer_11_out), .sel(B[0]));
  Multiplexer multiplexer_12 (.in0(A[11]), .in1(A[10]), .out(multiplexer_12_out), .sel(B[0]));
  Multiplexer multiplexer_13 (.in0(A[12]), .in1(A[11]), .out(multiplexer_13_out), .sel(B[0]));
  Multiplexer multiplexer_14 (.in0(A[13]), .in1(A[12]), .out(multiplexer_14_out), .sel(B[0]));
  Multiplexer multiplexer_15 (.in0(A[14]), .in1(A[13]), .out(multiplexer_15_out), .sel(B[0]));
  Multiplexer multiplexer_16 (.in0(A[15]), .in1(A[14]), .out(multiplexer_16_out), .sel(B[0]));
  Multiplexer multiplexer_17 (.in0(multiplexer_1_out), .in1(1'b0), .out(multiplexer_17_out), .sel(B[1]));
  Multiplexer multiplexer_18 (.in0(multiplexer_2_out), .in1(1'b0), .out(multiplexer_18_out), .sel(B[1]));
  Multiplexer multiplexer_19 (.in0(multiplexer_3_out), .in1(multiplexer_1_out), .out(multiplexer_19_out), .sel(B[1]));
  Multiplexer multiplexer_20 (.in0(multiplexer_4_out), .in1(multiplexer_2_out), .out(multiplexer_20_out), .sel(B[1]));
  Multiplexer multiplexer_21 (.in0(multiplexer_5_out), .in1(multiplexer_3_out), .out(multiplexer_21_out), .sel(B[1]));
  Multiplexer multiplexer_22 (.in0(multiplexer_6_out), .in1(multiplexer_4_out), .out(multiplexer_22_out), .sel(B[1]));
  Multiplexer multiplexer_23 (.in0(multiplexer_7_out), .in1(multiplexer_5_out), .out(multiplexer_23_out), .sel(B[1]));
  Multiplexer multiplexer_24 (.in0(multiplexer_8_out), .in1(multiplexer_6_out), .out(multiplexer_24_out), .sel(B[1]));
  Multiplexer multiplexer_25 (.in0(multiplexer_9_out), .in1(multiplexer_7_out), .out(multiplexer_25_out), .sel(B[1]));
  Multiplexer multiplexer_26 (.in0(multiplexer_10_out), .in1(multiplexer_8_out), .out(multiplexer_26_out), .sel(B[1]));
  Multiplexer multiplexer_27 (.in0(multiplexer_11_out), .in1(multiplexer_9_out), .out(multiplexer_27_out), .sel(B[1]));
  Multiplexer multiplexer_28 (.in0(multiplexer_12_out), .in1(multiplexer_10_out), .out(multiplexer_28_out), .sel(B[1]));
  Multiplexer multiplexer_29 (.in0(multiplexer_13_out), .in1(multiplexer_11_out), .out(multiplexer_29_out), .sel(B[1]));
  Multiplexer multiplexer_30 (.in0(multiplexer_14_out), .in1(multiplexer_12_out), .out(multiplexer_30_out), .sel(B[1]));
  Multiplexer multiplexer_31 (.in0(multiplexer_15_out), .in1(multiplexer_13_out), .out(multiplexer_31_out), .sel(B[1]));
  Multiplexer multiplexer_32 (.in0(multiplexer_16_out), .in1(multiplexer_14_out), .out(multiplexer_32_out), .sel(B[1]));
  Multiplexer multiplexer_33 (.in0(multiplexer_17_out), .in1(1'b0), .out(multiplexer_33_out), .sel(B[2]));
  Multiplexer multiplexer_34 (.in0(multiplexer_18_out), .in1(1'b0), .out(multiplexer_34_out), .sel(B[2]));
  Multiplexer multiplexer_35 (.in0(multiplexer_19_out), .in1(1'b0), .out(multiplexer_35_out), .sel(B[2]));
  Multiplexer multiplexer_36 (.in0(multiplexer_20_out), .in1(1'b0), .out(multiplexer_36_out), .sel(B[2]));
  Multiplexer multiplexer_37 (.in0(multiplexer_21_out), .in1(multiplexer_17_out), .out(multiplexer_37_out), .sel(B[2]));
  Multiplexer multiplexer_38 (.in0(multiplexer_22_out), .in1(multiplexer_18_out), .out(multiplexer_38_out), .sel(B[2]));
  Multiplexer multiplexer_39 (.in0(multiplexer_23_out), .in1(multiplexer_19_out), .out(multiplexer_39_out), .sel(B[2]));
  Multiplexer multiplexer_40 (.in0(multiplexer_24_out), .in1(multiplexer_20_out), .out(multiplexer_40_out), .sel(B[2]));
  Multiplexer multiplexer_41 (.in0(multiplexer_25_out), .in1(multiplexer_21_out), .out(multiplexer_41_out), .sel(B[2]));
  Multiplexer multiplexer_42 (.in0(multiplexer_26_out), .in1(multiplexer_22_out), .out(multiplexer_42_out), .sel(B[2]));
  Multiplexer multiplexer_43 (.in0(multiplexer_27_out), .in1(multiplexer_23_out), .out(multiplexer_43_out), .sel(B[2]));
  Multiplexer multiplexer_44 (.in0(multiplexer_28_out), .in1(multiplexer_24_out), .out(multiplexer_44_out), .sel(B[2]));
  Multiplexer multiplexer_45 (.in0(multiplexer_29_out), .in1(multiplexer_25_out), .out(multiplexer_45_out), .sel(B[2]));
  Multiplexer multiplexer_46 (.in0(multiplexer_30_out), .in1(multiplexer_26_out), .out(multiplexer_46_out), .sel(B[2]));
  Multiplexer multiplexer_47 (.in0(multiplexer_31_out), .in1(multiplexer_27_out), .out(multiplexer_47_out), .sel(B[2]));
  Multiplexer multiplexer_48 (.in0(multiplexer_32_out), .in1(multiplexer_29_out), .out(multiplexer_48_out), .sel(B[2]));
  Multiplexer multiplexer_49 (.in0(multiplexer_33_out), .in1(1'b0), .out(result[0]), .sel(B[3]));
  Multiplexer multiplexer_50 (.in0(multiplexer_34_out), .in1(1'b0), .out(result[1]), .sel(B[3]));
  Multiplexer multiplexer_51 (.in0(multiplexer_35_out), .in1(1'b0), .out(result[2]), .sel(B[3]));
  Multiplexer multiplexer_52 (.in0(multiplexer_36_out), .in1(1'b0), .out(result[3]), .sel(B[3]));
  Multiplexer multiplexer_53 (.in0(multiplexer_37_out), .in1(1'b0), .out(result[4]), .sel(B[3]));
  Multiplexer multiplexer_54 (.in0(multiplexer_38_out), .in1(1'b0), .out(result[5]), .sel(B[3]));
  Multiplexer multiplexer_55 (.in0(multiplexer_39_out), .in1(1'b0), .out(result[6]), .sel(B[3]));
  Multiplexer multiplexer_56 (.in0(multiplexer_40_out), .in1(1'b0), .out(result[7]), .sel(B[3]));
  Multiplexer multiplexer_57 (.in0(multiplexer_41_out), .in1(multiplexer_33_out), .out(result[8]), .sel(B[3]));
  Multiplexer multiplexer_58 (.in0(multiplexer_42_out), .in1(multiplexer_34_out), .out(result[9]), .sel(B[3]));
  Multiplexer multiplexer_59 (.in0(multiplexer_43_out), .in1(multiplexer_35_out), .out(result[10]), .sel(B[3]));
  Multiplexer multiplexer_60 (.in0(multiplexer_44_out), .in1(multiplexer_36_out), .out(result[11]), .sel(B[3]));
  Multiplexer multiplexer_61 (.in0(multiplexer_45_out), .in1(multiplexer_37_out), .out(result[12]), .sel(B[3]));
  Multiplexer multiplexer_62 (.in0(multiplexer_46_out), .in1(multiplexer_38_out), .out(result[13]), .sel(B[3]));
  Multiplexer multiplexer_63 (.in0(multiplexer_47_out), .in1(multiplexer_39_out), .out(result[14]), .sel(B[3]));
  Multiplexer multiplexer_64 (.in0(multiplexer_48_out), .in1(multiplexer_40_out), .out(result[15]), .sel(B[3]));
endmodule

module mux2to8_r (
  input  s,
  input  [7:0] A,
  input  [7:0] B,
  output [7:0] result
);

  BusMux2way busmux2way_1 (.S(s), .increment(A[3:0]), .Branch(B[3:0]), .result(result[3:0]));
  BusMux2way busmux2way_2 (.S(s), .increment(A[7:4]), .Branch(B[7:4]), .result(result[7:4]));
endmodule

module mux2to16_r (
  input  S,
  input  [15:0] A,
  input  [15:0] B,
  output [15:0] RESUlt
);

  mux2to8_r mux2to8_r_1 (.s(S), .A(A[7:0]), .B(B[7:0]), .result(RESUlt[7:0]));
  mux2to8_r mux2to8_r_2 (.s(S), .A(A[15:8]), .B(B[15:8]), .result(RESUlt[15:8]));
endmodule

module ALU_16bit (
  input  [15:0] A,
  input  [15:0] B,
  input  sel_add,
  input  sel_sub,
  input  sel_xor,
  input  sel_and,
  input  sel_r,
  input  sel_l,
  input  B_pass,
  output [15:0] result,
  output zero,
  output postive
);

  wire not_2_out, or_1_out;
  wire [15:0] adder_16_1_sum, and_16_1_and_result, hotmux_16_1_result, lshift_16_1_result,
       rshift_16_1_result, sub_16_1_sub, xor_16_1_xor_result;

  // Probe on A
  // Probe on B
  Adder_16 adder_16_1 (.A(A), .B(B), .sum(adder_16_1_sum));  // open: carry_in, carrry_out
  Sub_16 sub_16_1 (.A(A), .B(B), .sub(sub_16_1_sub));  // open: cRRY_OUT
  XOR_16 xor_16_1 (.A(A), .B(B), .xor_result(xor_16_1_xor_result));
  AND_16 and_16_1 (.A(A), .B(B), .AND_result(and_16_1_and_result));
  rshift_16 rshift_16_1 (.A(A), .B(B), .result(rshift_16_1_result));
  Lshift_16 lshift_16_1 (.A(A), .B(B), .result(lshift_16_1_result));
  Hotmux_16 hotmux_16_1 (
    .sel_add(sel_add), .sel_sub(sel_sub), .sel_xor(sel_xor), .sel_and(sel_and), .sel_r(sel_r), .sel_l(sel_l),
    .ADD(adder_16_1_sum), .SUB(sub_16_1_sub), .XOR_in(xor_16_1_xor_result), .AND_IN(and_16_1_and_result),
    .R_shift(rshift_16_1_result), .L_shift(lshift_16_1_result), .result(hotmux_16_1_result));
  // Probe on result
  or or_1 (or_1_out, result[0], result[1], result[2], result[3], result[4], result[5], result[6], result[7], result[8], result[9], result[10], result[11], result[12], result[13], result[14], result[15]);
  not not_1 (zero, or_1_out);
  not not_2 (not_2_out, result[15]);
  mux2to16_r mux2to16_r_1 (.S(B_pass), .A(hotmux_16_1_result), .B(B), .RESUlt(result));
  and and_1 (postive, or_1_out, not_2_out);
endmodule

module phase_generator16 (
  input  CLK,
  input  halt,
  output Fetch,
  output fetch_w,
  output execute,
  output execute_w
);

  wire and_1_out, and_3_out, not_1_out, not_2_out, not_3_out;
  wire [1:0] register_1_q, xor_2_out;

  // Probe on xor_2_out
  Register #(.width(2)) register_1 (.D(xor_2_out), .en(not_1_out), .clk(and_1_out), .Q(register_1_q), .clr(1'b0));
  not not_1 (not_1_out, halt);
  and and_1 (and_1_out, CLK, not_1_out);
  // AND_Gate and_2 has open pins: in0=register_1_q[1], in1=and_3_out, out=open
  xor xor_1 (xor_2_out[1], and_3_out, register_1_q[1]);
  xor xor_2 (xor_2_out[0], register_1_q[0], 1'b1);
  and and_3 (and_3_out, register_1_q[0], 1'b1);
  not not_2 (not_2_out, register_1_q[0]);
  not not_3 (not_3_out, register_1_q[1]);
  and and_4 (Fetch, not_2_out, not_3_out);
  and and_5 (fetch_w, not_3_out, register_1_q[0]);
  and and_6 (execute, register_1_q[1], not_2_out);
  and and_7 (execute_w, register_1_q[1], register_1_q[0]);
  // Probe on nothing
endmodule

module registerfile_16 (
  input  clk,
  input  [3:0] rs_addr,
  input  [3:0] rt_addr,
  input  [3:0] rd_addr,
  input  [15:0] data,
  input  reg_write,
  input  Read_Rd_Mux,
  output [15:0] rs_data,
  output [15:0] rt_data
);

  wire and_1_out, or_1_out;
  wire [3:0] multiplexer_1_out, multiplexer_2_out, multiplexer_3_out;

  or or_1 (or_1_out, rd_addr[0], rd_addr[1], rd_addr[2], rd_addr[3]);
  Multiplexer #(.width(4)) multiplexer_1 (.in0(rs_addr), .in1(rd_addr), .out(multiplexer_1_out), .sel(reg_write));
  Multiplexer #(.width(4)) multiplexer_2 (.in0(rt_addr), .in1(rd_addr), .out(multiplexer_2_out), .sel(Read_Rd_Mux));
  and and_1 (and_1_out, or_1_out, reg_write);
  Multiplexer #(.width(4)) multiplexer_3 (
    .in0(multiplexer_2_out), .in1(rd_addr), .out(multiplexer_3_out), .sel(reg_write));
  RAM #(.addrWidth(4), .dataWidth(16)) RS (
    .addr(multiplexer_1_out), .we(and_1_out), .clk(clk), .din(data), .dout(rs_data));  // open: oe
  RAM #(.addrWidth(4), .dataWidth(16)) RT (
    .addr(multiplexer_3_out), .we(and_1_out), .clk(clk), .din(data), .dout(rt_data));  // open: oe

  // Notes on the sheet:
  //   RS
  //   RT
endmodule

module memory_16 (
  input  w_enable,
  input  [7:0] Address,
  input  CLK,
  input  [15:0] Data_in,
  input  in_5,
  output [15:0] Data_out
);

  // Probe on Address
  RAM #(.clearpin("true"), .dataWidth(16), .\type ("nonvolatile")) ram_1 (
    .addr(Address), .we(w_enable), .clk(CLK), .din(Data_in), .dout(Data_out), .clr(in_5));  // open: oe
endmodule

module PC_16 (
  input  pc_enable,
  input  load,
  input  [7:0] Jump_add,
  input  clk,
  output [7:0] Q
);

  wire [7:0] incrementer4bit_1_r, mux2to8_r_1_result;

  Register register_1 (.D(mux2to8_r_1_result), .en(pc_enable), .clk(clk), .Q(Q));  // open: clr
  Incrementer4bit incrementer4bit_1 (.PC_input(Q), .r(incrementer4bit_1_r));
  mux2to8_r mux2to8_r_1 (.s(load), .A(incrementer4bit_1_r), .B(Jump_add), .result(mux2to8_r_1_result));
  // Probe on Q
endmodule

module IR_r (
  input  [15:0] data,
  input  we,
  input  clk,
  output [3:0] opcode,
  output [3:0] T,
  output [3:0] S,
  output [3:0] D,
  output [7:0] addr
);

  Register #(.width(16)) register_1 (.D(data), .en(we), .clk(clk), .Q({opcode, D, addr}), .clr(1'b0));
  // Probe on addr

  assign S = addr[7:4];
  assign T = addr[3:0];
endmodule

// ADD
module CU_r (
  input  execute_w,
  input  execute,
  input  fetch_w,
  input  fetch,
  input  [3:0] Opcode,
  input  zero,
  input  postive,
  output halt,
  output ADD,
  output SUB,
  output AND_D,
  output XOR_D,
  output L_shift,
  output R_shift,
  output Read_rd_mux,
  output [1:0] mem_addr_mux,
  output ALU_b_mux,
  output write_mem,
  output [1:0] reg_W_src,
  output pc_load,
  output pc_src_mux,
  output reg_w,
  output IR_w,
  output pc_w,
  output B_pc
);

  wire and_1_out, and_2_out, and_4_out, and_5_out, not_1_out, or_1_out, or_3_out, or_4_out, or_5_out,
       or_7_out, or_8_out, or_9_out, or_12_out;
  wire [13:0] decorder_1_result;

  decorder decorder_1 (
    .Opcode(Opcode),
    .result({reg_W_src[1], pc_src_mux, decorder_1_result[13:7], R_shift, L_shift, XOR_D, AND_D, SUB, ADD, decorder_1_result[0]}));
  and and_1 (and_1_out, postive, decorder_1_result[13]);
  and and_2 (and_2_out, zero, decorder_1_result[12]);
  or or_1 (or_1_out, and_1_out, pc_src_mux, reg_W_src[1], and_2_out);
  or or_2 (B_pc, decorder_1_result[7], decorder_1_result[12], decorder_1_result[13]);
  and and_3 (halt, execute_w, decorder_1_result[0]);
  or or_3 (or_3_out, decorder_1_result[8], decorder_1_result[9]);
  or or_4 (or_4_out, decorder_1_result[10], decorder_1_result[11]);
  and and_4 (and_4_out, L_shift, execute_w);
  and and_5 (and_5_out, execute_w, R_shift);
  or or_5 (or_5_out, decorder_1_result[9], decorder_1_result[12], decorder_1_result[13], pc_src_mux, decorder_1_result[11]);
  or or_6 (reg_W_src[0], decorder_1_result[10], decorder_1_result[8]);
  or or_7 (or_7_out, fetch_w, fetch);
  not not_1 (not_1_out, or_7_out);
  or or_8 (or_8_out, and_4_out, and_5_out);
  and and_6 (mem_addr_mux[0], or_3_out, not_1_out);
  and and_7 (mem_addr_mux[1], not_1_out, or_4_out);
  or or_9 (or_9_out, decorder_1_result[9], decorder_1_result[11]);
  or or_10 (Read_rd_mux, or_8_out, or_5_out);
  or or_11 (ALU_b_mux, or_3_out, decorder_1_result[7]);
  and and_8 (pc_load, or_1_out, execute_w);
  and and_9 (write_mem, execute_w, or_9_out);
  or or_12 (or_12_out, ADD, SUB, AND_D, XOR_D, L_shift, R_shift, decorder_1_result[7], decorder_1_result[8], decorder_1_result[10], reg_W_src[1]);
  and and_10 (reg_w, or_12_out, execute_w);
  or or_13 (pc_w, fetch_w, pc_load);

  assign IR_w = fetch_w;
endmodule

module CPU_r (
);

  wire alu_16bit_1_postive, alu_16bit_1_zero, clock_1_out, cu_add, cu_alu_b_mux, cu_and_d, cu_b_pc, cu_halt,
       cu_ir_w, cu_l_shift, cu_pc_load, cu_pc_src_mux, cu_pc_w, cu_r_shift, cu_read_rd_mux, cu_reg_w, cu_sub,
       cu_write_mem, cu_xor_d, phase_generator16_1_execute, phase_generator16_1_execute_w,
       phase_generator16_1_fetch, phase_generator16_1_fetch_w;
  wire [1:0] cu_mem_addr_mux, cu_reg_w_src;
  wire [3:0] ir_r_1_d, ir_r_1_opcode, ir_r_1_s, ir_r_1_t;
  wire [7:0] ir_r_1_addr, mux2to8_r_1_result, pc_16_1_q, registerfile_16_1_rt_data,
       registerfile_16_1_rt_data_2, select_me_ad_result;
  wire [15:0] alu_16bit_1_result, memory_16_1_data_out, mux2to16_r_1_result, r_mux16_1_result, register_1_q,
       registerfile_16_1_rs_data;

  Clock clock_1 (.out(clock_1_out));
  phase_generator16 phase_generator16_1 (
    .CLK(clock_1_out), .halt(cu_halt), .Fetch(phase_generator16_1_fetch),
    .fetch_w(phase_generator16_1_fetch_w), .execute(phase_generator16_1_execute),
    .execute_w(phase_generator16_1_execute_w));
  IR_r ir_r_1 (
    .data(memory_16_1_data_out), .we(cu_ir_w), .clk(clock_1_out), .opcode(ir_r_1_opcode), .T(ir_r_1_t),
    .S(ir_r_1_s), .D(ir_r_1_d), .addr(ir_r_1_addr));
  Register #(.trigger("high"), .width(16)) register_1 (
    .D(r_mux16_1_result), .en(1'b1), .clk(clock_1_out), .Q(register_1_q));  // open: clr
  registerfile_16 registerfile_16_1 (
    .clk(clock_1_out), .rs_addr(ir_r_1_s), .rt_addr(ir_r_1_t), .rd_addr(ir_r_1_d), .data(register_1_q),
    .reg_write(cu_reg_w), .Read_Rd_Mux(cu_read_rd_mux), .rs_data(registerfile_16_1_rs_data),
    .rt_data({registerfile_16_1_rt_data_2, registerfile_16_1_rt_data}));
  mux2to8_r mux2to8_r_1 (
    .s(cu_pc_src_mux), .A(ir_r_1_addr), .B(registerfile_16_1_rt_data), .result(mux2to8_r_1_result));
  CU_r cu (
    .execute_w(phase_generator16_1_execute_w), .execute(phase_generator16_1_execute),
    .fetch_w(phase_generator16_1_fetch_w), .fetch(phase_generator16_1_fetch), .Opcode(ir_r_1_opcode),
    .zero(alu_16bit_1_zero), .postive(alu_16bit_1_postive), .halt(cu_halt), .ADD(cu_add), .SUB(cu_sub),
    .AND_D(cu_and_d), .XOR_D(cu_xor_d), .L_shift(cu_l_shift), .R_shift(cu_r_shift),
    .Read_rd_mux(cu_read_rd_mux), .mem_addr_mux(cu_mem_addr_mux), .ALU_b_mux(cu_alu_b_mux),
    .write_mem(cu_write_mem), .reg_W_src(cu_reg_w_src), .pc_load(cu_pc_load), .pc_src_mux(cu_pc_src_mux),
    .reg_w(cu_reg_w), .IR_w(cu_ir_w), .pc_w(cu_pc_w), .B_pc(cu_b_pc));
  mux2to16_r mux2to16_r_1 (
    .S(cu_alu_b_mux), .A({registerfile_16_1_rt_data_2, registerfile_16_1_rt_data}),
    .B({{8{1'b0}}, ir_r_1_addr}), .RESUlt(mux2to16_r_1_result));
  PC_16 pc_16_1 (
    .pc_enable(cu_pc_w), .load(cu_pc_load), .Jump_add(mux2to8_r_1_result), .clk(clock_1_out), .Q(pc_16_1_q));
  ALU_16bit alu_16bit_1 (
    .A(registerfile_16_1_rs_data), .B(mux2to16_r_1_result), .sel_add(cu_add), .sel_sub(cu_sub),
    .sel_xor(cu_xor_d), .sel_and(cu_and_d), .sel_r(cu_r_shift), .sel_l(cu_l_shift), .B_pass(cu_b_pc),
    .result(alu_16bit_1_result), .zero(alu_16bit_1_zero), .postive(alu_16bit_1_postive));
  Amux_8bit select_me_ad (
    .A(pc_16_1_q), .B(ir_r_1_addr), .c(registerfile_16_1_rs_data[7:0]), .s(cu_mem_addr_mux),
    .result(select_me_ad_result));
  memory_16 memory_16_1 (
    .w_enable(cu_write_mem), .Address(select_me_ad_result), .CLK(clock_1_out),
    .Data_in({registerfile_16_1_rt_data_2, registerfile_16_1_rt_data}), .Data_out(memory_16_1_data_out));  // open: in_5
  R_mux16 r_mux16_1 (
    .ALU(alu_16bit_1_result), .MEM(memory_16_1_data_out), .pc_incre({{8{1'b0}}, pc_16_1_q}),
    .s(cu_reg_w_src), .result(r_mux16_1_result));
endmodule
